// Logisim project 2-1MUX.circ as structural Verilog: 2 circuits, main circuit main
module main (
  input  a0,
  input  in_2,
  input  in_3,
  input  a3,
  input  s0,
  input  s1,
  output out_7
);

  wire n2_1mux_1_o1, n2_1mux_2_o1;

  _2_1MUX u_2_1mux_1 (.a0(a0), .a1(in_2), .s(s0), .o1(n2_1mux_1_o1));
  _2_1MUX u_2_1mux_2 (.a0(in_3), .a1(a3), .s(s0), .o1(n2_1mux_2_o1));
  _2_1MUX u_2_1mux_3 (.a0(n2_1mux_1_o1), .a1(n2_1mux_2_o1), .s(s1), .o1(out_7));
endmodule

module _2_1MUX (
  input  a0,
  input  a1,
  input  s,
  output o1
);

  wire and_1_out, and_2_out, not_1_out;

  not not_1 (not_1_out, s);
  and and_1 (and_1_out, a0, not_1_out);
  and and_2 (and_2_out, a1, s);
  or or_1 (o1, and_1_out, and_2_out);
endmodule
