// Logisim project hw1-counter4bit.circ as structural Verilog: 1 circuit, main circuit main
module main (
  input  x,
  output o3,
  output o2,
  output o1,
  output o0
);

  wire and_1_out, and_2_out, and_3_out, and_4_out, and_5_out, clock_1_out, not_1_out, or_1_out, or_2_out,
       T0_qn, T1_qn, T2_qn, T3_qn, xnor_1_out, xor_1_out;

  not not_1 (not_1_out, x);
  and and_1 (and_1_out, T2_qn, T1_qn, T0_qn, x);
  and and_2 (and_2_out, T3_qn, o2, o1, o0, not_1_out);
  and and_3 (and_3_out, o3, o2, T1_qn, o0, not_1_out);
  or or_1 (or_1_out, and_1_out, and_2_out, and_3_out);
  and and_4 (and_4_out, o0, o1, not_1_out);
  and and_5 (and_5_out, T0_qn, T1_qn, x);
  or or_2 (or_2_out, and_4_out, and_5_out);
  xor xor_1 (xor_1_out, o0, x);
  NotExactlyOne xnor_1 (.out(xnor_1_out), .in0(o3), .in1(o2), .in2(o0));
  Clock clock_1 (.out(clock_1_out));
  T_Flip_Flop T3 (.clk(clock_1_out), .T(or_1_out), .Q(o3), .Qn(T3_qn));  // open: preset, reset, en
  T_Flip_Flop T2 (.clk(clock_1_out), .T(or_2_out), .Q(o2), .Qn(T2_qn));  // open: preset, reset, en
  T_Flip_Flop T1 (.clk(clock_1_out), .T(xor_1_out), .Q(o1), .Qn(T1_qn));  // open: preset, reset, en
  T_Flip_Flop T0 (.clk(clock_1_out), .T(xnor_1_out), .Q(o0), .Qn(T0_qn));  // open: preset, reset, en
endmodule
