// Logisim project 1bit_add.circ as structural Verilog: 6 circuits, main circuit 1bit_add
module _1bit_add (
  input  c_in,
  input  a,
  input  b,
  input  s1,
  input  s0,
  output out,
  output c_out
);

  wire multiplexer_1_out, not_1_out;

  not not_1 (not_1_out, b);
  Multiplexer #(.select(2)) multiplexer_1 (
    .in0(b), .in1(not_1_out), .in2(1'b0), .in3(1'b1), .out(multiplexer_1_out), .sel({s1, s0}));  // open: en
  Adder #(.width(1)) adder_1 (.a(a), .b(multiplexer_1_out), .out(out), .cin(c_in), .cout(c_out));
endmodule

module _2bit (
  input  in_1,
  input  a1,
  input  a0,
  input  b1,
  input  b0,
  input  in_6,
  input  in_7,
  output out_8,
  output s1,
  output s0
);

  wire n1bit_add_1_c_out;

  _1bit_add u_1bit_add_1 (.a(a0), .b(b0), .out(s0), .c_out(n1bit_add_1_c_out), .c_in(in_1), .s1(in_6), .s0(in_7));
  _1bit_add u_1bit_add_2 (.a(a1), .b(b1), .out(s1), .c_out(out_8), .c_in(n1bit_add_1_c_out), .s1(in_6), .s0(in_7));
endmodule

module _4bit (
  input  [3:0] a,
  input  [3:0] b,
  input  [1:0] s,
  input  cin,
  output cout,
  output [3:0] out
);

  wire n1bit_add_1_c_out, n1bit_add_2_c_out, n1bit_add_3_c_out;

  _1bit_add u_1bit_add_1 (
    .a(a[0]), .b(b[0]), .out(out[0]), .c_out(n1bit_add_1_c_out), .c_in(cin), .s1(s[1]), .s0(s[0]));
  _1bit_add u_1bit_add_2 (
    .a(a[1]), .b(b[1]), .out(out[1]), .c_out(n1bit_add_2_c_out), .c_in(n1bit_add_1_c_out), .s1(s[1]),
    .s0(s[0]));
  _1bit_add u_1bit_add_3 (
    .a(a[2]), .b(b[2]), .out(out[2]), .c_out(n1bit_add_3_c_out), .c_in(n1bit_add_2_c_out), .s1(s[1]),
    .s0(s[0]));
  _1bit_add u_1bit_add_4 (
    .a(a[3]), .b(b[3]), .out(out[3]), .c_out(cout), .c_in(n1bit_add_3_c_out), .s1(s[1]), .s0(s[0]));
endmodule

module asd (
);

  _4bit u_4bit_1 ();  // open: a, b, s, cin, cout, out
endmodule

module _2_1mux (
  input  in1,
  input  in0,
  input  s,
  output o
);

  wire nand_1_out, nand_2_out, not_1_out;

  nand nand_1 (nand_1_out, in1, not_1_out);
  not not_1 (not_1_out, s);
  nand nand_2 (nand_2_out, not_1_out, in0);
  nand nand_3 (o, nand_1_out, nand_2_out);
endmodule

module _4_1mux (
  input  i0,
  input  i1,
  input  i2,
  input  s0,
  input  i3,
  input  s1,
  output o
);

  wire n2_1mux_1_o, n2_1mux_2_o;

  _2_1mux u_2_1mux_1 (.in1(i1), .in0(i0), .o(n2_1mux_1_o), .s(s1));
  _2_1mux u_2_1mux_2 (.in1(i3), .in0(i2), .o(n2_1mux_2_o), .s(s1));
  _2_1mux u_2_1mux_3 (.in1(n2_1mux_2_o), .in0(n2_1mux_1_o), .o(o), .s(s0));
endmodule
