// Logisim project prj4-microprg.circ as structural Verilog: 17 circuits, main circuit d ff
module d_ff (
  input  d,
  input  en,
  output q,
  output q_prime
);

  wire and_1_out, and_2_out, not_1_out;

  not not_1 (not_1_out, d);
  and and_1 (and_1_out, not_1_out, en);
  and and_2 (and_2_out, en, d);
  nor nor_1 (q, and_1_out, q_prime);
  nor nor_2 (q_prime, q, and_2_out);
endmodule

module _1bit_register (
  input  cin,
  input  clr,
  input  in,
  input  incr,
  input  clk,
  input  Load,
  output cout,
  output q
);

  wire multiplexer_1_out, multiplexer_2_out, multiplexer_3_out, n2bit_adder_1_s;

  _2bit_adder u_2bit_adder_1 (.x(q), .y(1'b0), .cin(cin), .s(n2bit_adder_1_s), .cout(cout));
  Multiplexer multiplexer_1 (.in0(q), .in1(1'b0), .out(multiplexer_1_out), .sel(clr));  // open: en
  Multiplexer multiplexer_2 (
    .in0(multiplexer_1_out), .in1(n2bit_adder_1_s), .out(multiplexer_2_out), .sel(incr));  // open: en
  Multiplexer multiplexer_3 (.in0(multiplexer_2_out), .in1(in), .out(multiplexer_3_out), .sel(Load));  // open: en
  D_Flip_Flop d_ff_1 (.clk(clk), .D(multiplexer_3_out), .Q(q));  // open: Qn, preset, en, reset
endmodule

module _16bit_register (
  input  clk,
  input  [15:0] \input ,
  input  ld,
  input  inc,
  input  clr,
  output [15:0] out
);

  wire n1bit_register_1_cout, n1bit_register_2_cout, n1bit_register_3_cout, n1bit_register_4_cout,
       n1bit_register_5_cout, n1bit_register_6_cout, n1bit_register_7_cout, n1bit_register_8_cout,
       n1bit_register_9_cout, n1bit_register_10_cout, n1bit_register_11_cout, n1bit_register_12_cout,
       n1bit_register_13_cout, n1bit_register_14_cout, n1bit_register_15_cout, n1bit_register_16_cout;

  _1bit_register u_1bit_register_1 (
    .cin(inc), .clk(clk), .cout(n1bit_register_1_cout), .in(\input [0]), .clr(clr), .incr(inc), .Load(ld),
    .q(out[0]));
  _1bit_register u_1bit_register_2 (
    .cin(n1bit_register_1_cout), .clk(clk), .cout(n1bit_register_2_cout), .in(\input [1]), .clr(clr),
    .incr(inc), .Load(ld), .q(out[1]));
  _1bit_register u_1bit_register_3 (
    .cin(n1bit_register_2_cout), .clk(clk), .cout(n1bit_register_3_cout), .in(\input [2]), .clr(clr),
    .incr(inc), .Load(ld), .q(out[2]));
  _1bit_register u_1bit_register_4 (
    .cin(n1bit_register_3_cout), .clk(clk), .cout(n1bit_register_4_cout), .in(\input [3]), .clr(clr),
    .incr(inc), .Load(ld), .q(out[3]));
  _1bit_register u_1bit_register_5 (
    .cin(n1bit_register_4_cout), .clk(clk), .cout(n1bit_register_5_cout), .in(\input [4]), .clr(clr),
    .incr(inc), .Load(ld), .q(out[4]));
  _1bit_register u_1bit_register_6 (
    .cin(n1bit_register_5_cout), .clk(clk), .cout(n1bit_register_6_cout), .in(\input [5]), .clr(clr),
    .incr(inc), .Load(ld), .q(out[5]));
  _1bit_register u_1bit_register_7 (
    .cin(n1bit_register_6_cout), .clk(clk), .cout(n1bit_register_7_cout), .in(\input [6]), .clr(clr),
    .incr(inc), .Load(ld), .q(out[6]));
  _1bit_register u_1bit_register_8 (
    .cin(n1bit_register_7_cout), .clk(clk), .cout(n1bit_register_8_cout), .in(\input [7]), .clr(clr),
    .incr(inc), .Load(ld), .q(out[7]));
  _1bit_register u_1bit_register_9 (
    .cin(n1bit_register_8_cout), .clk(clk), .cout(n1bit_register_9_cout), .in(\input [8]), .clr(clr),
    .incr(inc), .Load(ld), .q(out[8]));
  _1bit_register u_1bit_register_10 (
    .cin(n1bit_register_9_cout), .clk(clk), .cout(n1bit_register_10_cout), .in(\input [9]), .clr(clr),
    .incr(inc), .Load(ld), .q(out[9]));
  _1bit_register u_1bit_register_11 (
    .cin(n1bit_register_10_cout), .clk(clk), .cout(n1bit_register_11_cout), .in(\input [10]), .clr(clr),
    .incr(inc), .Load(ld), .q(out[10]));
  _1bit_register u_1bit_register_12 (
    .cin(n1bit_register_11_cout), .clk(clk), .cout(n1bit_register_12_cout), .in(\input [11]), .clr(clr),
    .incr(inc), .Load(ld), .q(out[11]));
  _1bit_register u_1bit_register_13 (
    .cin(n1bit_register_12_cout), .clk(clk), .cout(n1bit_register_13_cout), .in(\input [12]), .clr(clr),
    .incr(inc), .Load(ld), .q(out[12]));
  _1bit_register u_1bit_register_14 (
    .cin(n1bit_register_13_cout), .clk(clk), .cout(n1bit_register_14_cout), .in(\input [13]), .clr(clr),
    .incr(inc), .Load(ld), .q(out[13]));
  _1bit_register u_1bit_register_15 (
    .cin(n1bit_register_14_cout), .clk(clk), .cout(n1bit_register_15_cout), .in(\input [14]), .clr(clr),
    .incr(inc), .Load(ld), .q(out[14]));
  _1bit_register u_1bit_register_16 (
    .cin(n1bit_register_15_cout), .clk(clk), .cout(n1bit_register_16_cout), .in(\input [15]), .clr(clr),
    .incr(inc), .Load(ld), .q(out[15]));
endmodule

module register_test (
  input  [15:0] \input ,
  input  [2:0] ld_inc_clr,
  output [15:0] \output 
);

  wire clock_1_out;

  Hex_Digit_Display hex_digit_display_1 (.value(\input [15:12]));  // open: dp
  Hex_Digit_Display hex_digit_display_2 (.value(\input [11:8]));  // open: dp
  Hex_Digit_Display hex_digit_display_3 (.value(\input [7:4]));  // open: dp
  Hex_Digit_Display hex_digit_display_4 (.value(\input [3:0]));  // open: dp
  _16bit_register u_16bit_register_1 (
    .clk(clock_1_out), .\input (\input ), .out(\output ), .ld(ld_inc_clr[2]), .inc(ld_inc_clr[1]),
    .clr(ld_inc_clr[0]));
  Clock clock_1 (.out(clock_1_out));
  Hex_Digit_Display hex_digit_display_5 (.value(\output [15:12]));  // open: dp
  Hex_Digit_Display hex_digit_display_6 (.value(\output [11:8]));  // open: dp
  Hex_Digit_Display hex_digit_display_7 (.value(\output [3:0]));  // open: dp
  Hex_Digit_Display hex_digit_display_8 (.value(\output [7:4]));  // open: dp
endmodule

module _12bit_register (
  input  clk,
  input  [11:0] \input ,
  input  ld,
  input  inc,
  input  clr,
  output [11:0] out
);

  wire n1bit_register_1_cout, n1bit_register_2_cout, n1bit_register_3_cout, n1bit_register_4_cout,
       n1bit_register_5_cout, n1bit_register_6_cout, n1bit_register_7_cout, n1bit_register_8_cout,
       n1bit_register_9_cout, n1bit_register_10_cout, n1bit_register_11_cout, n1bit_register_12_cout;

  _1bit_register u_1bit_register_1 (
    .cin(inc), .clk(clk), .cout(n1bit_register_1_cout), .in(\input [0]), .clr(clr), .incr(inc), .Load(ld),
    .q(out[0]));
  _1bit_register u_1bit_register_2 (
    .cin(n1bit_register_1_cout), .clk(clk), .cout(n1bit_register_2_cout), .in(\input [1]), .clr(clr),
    .incr(inc), .Load(ld), .q(out[1]));
  _1bit_register u_1bit_register_3 (
    .cin(n1bit_register_2_cout), .clk(clk), .cout(n1bit_register_3_cout), .in(\input [2]), .clr(clr),
    .incr(inc), .Load(ld), .q(out[2]));
  _1bit_register u_1bit_register_4 (
    .cin(n1bit_register_3_cout), .clk(clk), .cout(n1bit_register_4_cout), .in(\input [3]), .clr(clr),
    .incr(inc), .Load(ld), .q(out[3]));
  _1bit_register u_1bit_register_5 (
    .cin(n1bit_register_4_cout), .clk(clk), .cout(n1bit_register_5_cout), .in(\input [4]), .clr(clr),
    .incr(inc), .Load(ld), .q(out[4]));
  _1bit_register u_1bit_register_6 (
    .cin(n1bit_register_5_cout), .clk(clk), .cout(n1bit_register_6_cout), .in(\input [5]), .clr(clr),
    .incr(inc), .Load(ld), .q(out[5]));
  _1bit_register u_1bit_register_7 (
    .cin(n1bit_register_6_cout), .clk(clk), .cout(n1bit_register_7_cout), .in(\input [6]), .clr(clr),
    .incr(inc), .Load(ld), .q(out[6]));
  _1bit_register u_1bit_register_8 (
    .cin(n1bit_register_7_cout), .clk(clk), .cout(n1bit_register_8_cout), .in(\input [7]), .clr(clr),
    .incr(inc), .Load(ld), .q(out[7]));
  _1bit_register u_1bit_register_9 (
    .cin(n1bit_register_8_cout), .clk(clk), .cout(n1bit_register_9_cout), .in(\input [8]), .clr(clr),
    .incr(inc), .Load(ld), .q(out[8]));
  _1bit_register u_1bit_register_10 (
    .cin(n1bit_register_9_cout), .clk(clk), .cout(n1bit_register_10_cout), .in(\input [9]), .clr(clr),
    .incr(inc), .Load(ld), .q(out[9]));
  _1bit_register u_1bit_register_11 (
    .cin(n1bit_register_10_cout), .clk(clk), .cout(n1bit_register_11_cout), .in(\input [10]), .clr(clr),
    .incr(inc), .Load(ld), .q(out[10]));
  _1bit_register u_1bit_register_12 (
    .cin(n1bit_register_11_cout), .clk(clk), .cout(n1bit_register_12_cout), .in(\input [11]), .clr(clr),
    .incr(inc), .Load(ld), .q(out[11]));
endmodule

module _8bit_register (
  input  clk,
  input  [7:0] \input ,
  input  ld,
  input  inc,
  input  clr,
  output [7:0] out
);

  wire n1bit_register_1_cout, n1bit_register_2_cout, n1bit_register_3_cout, n1bit_register_4_cout,
       n1bit_register_5_cout, n1bit_register_6_cout, n1bit_register_7_cout, n1bit_register_8_cout;

  _1bit_register u_1bit_register_1 (
    .cin(inc), .clk(clk), .cout(n1bit_register_1_cout), .in(\input [0]), .clr(clr), .incr(inc), .Load(ld),
    .q(out[0]));
  _1bit_register u_1bit_register_2 (
    .cin(n1bit_register_1_cout), .clk(clk), .cout(n1bit_register_2_cout), .in(\input [1]), .clr(clr),
    .incr(inc), .Load(ld), .q(out[1]));
  _1bit_register u_1bit_register_3 (
    .cin(n1bit_register_2_cout), .clk(clk), .cout(n1bit_register_3_cout), .in(\input [2]), .clr(clr),
    .incr(inc), .Load(ld), .q(out[2]));
  _1bit_register u_1bit_register_4 (
    .cin(n1bit_register_3_cout), .clk(clk), .cout(n1bit_register_4_cout), .in(\input [3]), .clr(clr),
    .incr(inc), .Load(ld), .q(out[3]));
  _1bit_register u_1bit_register_5 (
    .cin(n1bit_register_4_cout), .clk(clk), .cout(n1bit_register_5_cout), .in(\input [4]), .clr(clr),
    .incr(inc), .Load(ld), .q(out[4]));
  _1bit_register u_1bit_register_6 (
    .cin(n1bit_register_5_cout), .clk(clk), .cout(n1bit_register_6_cout), .in(\input [5]), .clr(clr),
    .incr(inc), .Load(ld), .q(out[5]));
  _1bit_register u_1bit_register_7 (
    .cin(n1bit_register_6_cout), .clk(clk), .cout(n1bit_register_7_cout), .in(\input [6]), .clr(clr),
    .incr(inc), .Load(ld), .q(out[6]));
  _1bit_register u_1bit_register_8 (
    .cin(n1bit_register_7_cout), .clk(clk), .cout(n1bit_register_8_cout), .in(\input [7]), .clr(clr),
    .incr(inc), .Load(ld), .q(out[7]));
endmodule

module AR_PC_BUS2 (
  input  s,
  input  [11:0] in1,
  input  [11:0] in0,
  output [11:0] out
);

  _2_1mux u_2_1mux_1 (.in0(in0[0]), .s(s), .in1(in1[0]), .o(out[0]));
  _2_1mux u_2_1mux_2 (.in0(in0[1]), .s(s), .in1(in1[1]), .o(out[1]));
  _2_1mux u_2_1mux_3 (.in0(in0[2]), .s(s), .in1(in1[2]), .o(out[2]));
  _2_1mux u_2_1mux_4 (.in0(in0[3]), .s(s), .in1(in1[3]), .o(out[3]));
  _2_1mux u_2_1mux_5 (.in0(in0[4]), .s(s), .in1(in1[4]), .o(out[4]));
  _2_1mux u_2_1mux_6 (.in0(in0[5]), .s(s), .in1(in1[5]), .o(out[5]));
  _2_1mux u_2_1mux_7 (.in0(in0[6]), .s(s), .in1(in1[6]), .o(out[6]));
  _2_1mux u_2_1mux_8 (.in0(in0[7]), .s(s), .in1(in1[7]), .o(out[7]));
  _2_1mux u_2_1mux_9 (.in0(in0[8]), .s(s), .in1(in1[8]), .o(out[8]));
  _2_1mux u_2_1mux_10 (.in0(in0[9]), .s(s), .in1(in1[9]), .o(out[9]));
  _2_1mux u_2_1mux_11 (.in0(in0[10]), .s(s), .in1(in1[10]), .o(out[10]));
  _2_1mux u_2_1mux_12 (.in0(in0[11]), .s(s), .in1(in1[11]), .o(out[11]));
endmodule

module alu_ac_inprSelect (
  input  [7:0] in8bit,
  input  [15:0] in16bit,
  input  _16_8_select,
  output [15:0] out16bit
);

  _2_1mux u_2_1mux_1 (.in0(in16bit[0]), .s(_16_8_select), .in1(in8bit[0]), .o(out16bit[0]));
  _2_1mux u_2_1mux_2 (.in0(in16bit[1]), .s(_16_8_select), .in1(in8bit[1]), .o(out16bit[1]));
  _2_1mux u_2_1mux_3 (.in0(in16bit[2]), .s(_16_8_select), .in1(in8bit[2]), .o(out16bit[2]));
  _2_1mux u_2_1mux_4 (.in0(in16bit[3]), .s(_16_8_select), .in1(in8bit[3]), .o(out16bit[3]));
  _2_1mux u_2_1mux_5 (.in0(in16bit[4]), .s(_16_8_select), .in1(in8bit[4]), .o(out16bit[4]));
  _2_1mux u_2_1mux_6 (.in0(in16bit[5]), .s(_16_8_select), .in1(in8bit[5]), .o(out16bit[5]));
  _2_1mux u_2_1mux_7 (.in0(in16bit[6]), .s(_16_8_select), .in1(in8bit[6]), .o(out16bit[6]));
  _2_1mux u_2_1mux_8 (.in0(in16bit[7]), .s(_16_8_select), .in1(in8bit[7]), .o(out16bit[7]));
  _2_1mux u_2_1mux_9 (.in0(in16bit[8]), .s(_16_8_select), .in1(1'b0), .o(out16bit[8]));
  _2_1mux u_2_1mux_10 (.in0(in16bit[9]), .s(_16_8_select), .in1(1'b0), .o(out16bit[9]));
  _2_1mux u_2_1mux_11 (.in0(in16bit[10]), .s(_16_8_select), .in1(1'b0), .o(out16bit[10]));
  _2_1mux u_2_1mux_12 (.in0(in16bit[11]), .s(_16_8_select), .in1(1'b0), .o(out16bit[11]));
  _2_1mux u_2_1mux_13 (.in0(in16bit[12]), .s(_16_8_select), .in1(1'b0), .o(out16bit[12]));
  _2_1mux u_2_1mux_14 (.in0(in16bit[13]), .s(_16_8_select), .in1(1'b0), .o(out16bit[13]));
  _2_1mux u_2_1mux_15 (.in0(in16bit[14]), .s(_16_8_select), .in1(1'b0), .o(out16bit[14]));
  _2_1mux u_2_1mux_16 (.in0(in16bit[15]), .s(_16_8_select), .in1(1'b0), .o(out16bit[15]));
endmodule

module simple_computer (
  input  [2:0] s2_s1_s0,
  input  mem_en,
  input  mem_w_r,
  input  s3,
  input  in_5,
  input  in_6,
  input  in_7,
  input  in_8,
  input  in_9,
  input  in_10,
  input  in_11,
  input  in_12,
  input  in_13,
  input  alu_cin,
  input  ac_inpr_select,
  input  in_16,
  input  in_17,
  input  in_18,
  input  [3:0] alu_select,
  input  in_20,
  input  in_21,
  input  in_22,
  input  in_23,
  input  in_24,
  input  in_25,
  input  in_26,
  input  in_27,
  input  in_28,
  input  in_29,
  input  in_30,
  input  in_31,
  output E
);

  wire clock_1_out, not_1_out;
  wire [3:0] AC_out, AC_out_2, AC_out_3, AC_out_4, bus1_1_out_10, bus1_1_out_10_3, bus1_1_out_10_4;
  wire [7:0] INPR_out;
  wire [7:4] bus1_1_out_10_2;
  wire [11:0] AR_out, ar_pc_bus2_1_out, n12bit_register_1_out;
  wire [15:0] alu_ac_inprselect_1_out16bit, controlled_buffer_2_out, DR_out, IR_out, n16bit_alu_1_out,
       ram_1_data, TR_out;

  Clock clock_1 (.out(clock_1_out));
  _8bit_register INPR (.clk(clock_1_out), .out(INPR_out), .ld(in_20), .inc(in_21), .clr(in_22));  // open: input
  Hex_Digit_Display hex_digit_display_1 (.value(bus1_1_out_10_4));  // open: dp
  Hex_Digit_Display hex_digit_display_2 (.value(bus1_1_out_10_3));  // open: dp
  _16bit_register IR (
    .clk(clock_1_out), .\input ({bus1_1_out_10_4, bus1_1_out_10_3, bus1_1_out_10_2, bus1_1_out_10}),
    .out(IR_out), .ld(in_23), .inc(in_24), .clr(in_25));
  Hex_Digit_Display hex_digit_display_3 (.value(bus1_1_out_10_2));  // open: dp
  Hex_Digit_Display hex_digit_display_4 (.value(bus1_1_out_10));  // open: dp
  _12bit_register AR (
    .clk(clock_1_out), .\input ({bus1_1_out_10_3, bus1_1_out_10_2, bus1_1_out_10}), .out(AR_out), .ld(in_5),
    .inc(in_6), .clr(in_7));
  _12bit_register u_12bit_register_1 (
    .clk(clock_1_out), .\input ({bus1_1_out_10_3, bus1_1_out_10_2, bus1_1_out_10}),
    .out(n12bit_register_1_out), .ld(in_8), .inc(in_9), .clr(in_10));
  _16bit_register DR (
    .clk(clock_1_out), .\input ({bus1_1_out_10_4, bus1_1_out_10_3, bus1_1_out_10_2, bus1_1_out_10}),
    .out(DR_out), .ld(in_11), .inc(in_12), .clr(in_13));
  alu_ac_inprSelect alu_ac_inprselect_1 (
    .in16bit({AC_out_4, AC_out_3, AC_out_2, AC_out}), .in8bit(INPR_out), ._16_8_select(ac_inpr_select),
    .out16bit(alu_ac_inprselect_1_out16bit));
  RAM #(.addrWidth(12), .dataWidth(16)) ram_1 (
    .addr(ar_pc_bus2_1_out), .data(ram_1_data), .sel(mem_en), .clk(clock_1_out), .ld(mem_w_r));  // open: clr
  not not_1 (not_1_out, mem_w_r);
  Hex_Digit_Display hex_digit_display_5 (.value(AC_out_4));  // open: dp
  _16bit_alu u_16bit_alu_1 (
    .out(n16bit_alu_1_out), .c_out(E), .a(DR_out), .b(alu_ac_inprselect_1_out16bit), .s(alu_select),
    .c_in(alu_cin));
  _16bit_register TR (
    .clk(clock_1_out), .\input ({bus1_1_out_10_4, bus1_1_out_10_3, bus1_1_out_10_2, bus1_1_out_10}),
    .out(TR_out), .ld(in_26), .inc(in_27), .clr(in_28));
  assign ram_1_data = not_1_out ? {bus1_1_out_10_4, bus1_1_out_10_3, bus1_1_out_10_2, bus1_1_out_10} : 16'bz;  // Controlled_Buffer controlled_buffer_1
  assign controlled_buffer_2_out = mem_w_r ? ram_1_data : 16'bz;  // Controlled_Buffer controlled_buffer_2
  AR_PC_BUS2 ar_pc_bus2_1 (.in1(n12bit_register_1_out), .in0(AR_out), .s(s3), .out(ar_pc_bus2_1_out));
  Hex_Digit_Display hex_digit_display_6 (.value(AC_out_2));  // open: dp
  Hex_Digit_Display hex_digit_display_7 (.value(AC_out_3));  // open: dp
  Hex_Digit_Display hex_digit_display_8 (.value(AC_out));  // open: dp
  _16bit_register AC (
    .clk(clock_1_out), .\input (n16bit_alu_1_out), .out({AC_out_4, AC_out_3, AC_out_2, AC_out}), .ld(in_16),
    .inc(in_17), .clr(in_18));
  _8bit_register OUTR (
    .clk(clock_1_out), .\input ({bus1_1_out_10_2, bus1_1_out_10}), .ld(in_29), .inc(in_30), .clr(in_31));  // open: out
  bus1 bus1_1 (
    .in_9(s2_s1_s0), .out_10({bus1_1_out_10_4, bus1_1_out_10_3, bus1_1_out_10_2, bus1_1_out_10}),
    ._0({16{1'b0}}), ._1(AR_out), ._2(n12bit_register_1_out), ._3(DR_out),
    ._4({AC_out_4, AC_out_3, AC_out_2, AC_out}), ._5(IR_out), ._6(TR_out), ._7(controlled_buffer_2_out));
endmodule

module _8_1mux (
  input  _0,
  input  _1,
  input  _2,
  input  _3,
  input  _4,
  input  _5,
  input  s2,
  input  _6,
  input  _7,
  input  s1,
  input  s0,
  output o
);

  wire n4_1mux_1_out_7, n4_1mux_2_out_7;

  _4_1mux u_4_1mux_1 (._0(_0), ._1(_1), ._2(_2), ._3(_3), .out_7(n4_1mux_1_out_7), .s0(s0), .s1(s1));
  _4_1mux u_4_1mux_2 (._0(_4), ._1(_5), ._2(_6), ._3(_7), .out_7(n4_1mux_2_out_7), .s0(s0), .s1(s1));
  _2_1mux u_2_1mux_1 (.in0(n4_1mux_1_out_7), .s(s2), .in1(n4_1mux_2_out_7), .o(o));
endmodule

module bus1 (
  input  [15:0] _0,
  input  [11:0] _1,
  input  [11:0] _2,
  input  [15:0] _3,
  input  [15:0] _4,
  input  [15:0] _5,
  input  [15:0] _6,
  input  [15:0] _7,
  input  [2:0] in_9,
  output [15:0] out_10
);

  wire decoder_1_out0, decoder_1_out1, decoder_1_out2, decoder_1_out3, decoder_1_out4, decoder_1_out5,
       decoder_1_out6, decoder_1_out7;

  Decoder #(.select(3)) decoder_1 (
    .out0(decoder_1_out0), .out1(decoder_1_out1), .out2(decoder_1_out2), .out3(decoder_1_out3),
    .out4(decoder_1_out4), .out5(decoder_1_out5), .out6(decoder_1_out6), .out7(decoder_1_out7), .sel(in_9));  // open: en
  assign out_10[15] = decoder_1_out0 ? _0[15] : 1'bz;  // Controlled_Buffer controlled_buffer_1
  assign out_10[14] = decoder_1_out0 ? _0[14] : 1'bz;  // Controlled_Buffer controlled_buffer_2
  assign out_10[13] = decoder_1_out0 ? _0[13] : 1'bz;  // Controlled_Buffer controlled_buffer_3
  assign out_10[12] = decoder_1_out0 ? _0[12] : 1'bz;  // Controlled_Buffer controlled_buffer_4
  assign out_10[11] = decoder_1_out0 ? _0[11] : 1'bz;  // Controlled_Buffer controlled_buffer_5
  assign out_10[10] = decoder_1_out0 ? _0[10] : 1'bz;  // Controlled_Buffer controlled_buffer_6
  assign out_10[9] = decoder_1_out0 ? _0[9] : 1'bz;  // Controlled_Buffer controlled_buffer_7
  assign out_10[8] = decoder_1_out0 ? _0[8] : 1'bz;  // Controlled_Buffer controlled_buffer_8
  assign out_10[7] = decoder_1_out0 ? _0[7] : 1'bz;  // Controlled_Buffer controlled_buffer_9
  assign out_10[6] = decoder_1_out0 ? _0[6] : 1'bz;  // Controlled_Buffer controlled_buffer_10
  assign out_10[5] = decoder_1_out0 ? _0[5] : 1'bz;  // Controlled_Buffer controlled_buffer_11
  assign out_10[4] = decoder_1_out0 ? _0[4] : 1'bz;  // Controlled_Buffer controlled_buffer_12
  assign out_10[3] = decoder_1_out0 ? _0[3] : 1'bz;  // Controlled_Buffer controlled_buffer_13
  assign out_10[2] = decoder_1_out0 ? _0[2] : 1'bz;  // Controlled_Buffer controlled_buffer_14
  assign out_10[1] = decoder_1_out0 ? _0[1] : 1'bz;  // Controlled_Buffer controlled_buffer_15
  assign out_10[0] = decoder_1_out0 ? _0[0] : 1'bz;  // Controlled_Buffer controlled_buffer_16
  assign out_10[15] = decoder_1_out1 ? 1'b0 : 1'bz;  // Controlled_Buffer controlled_buffer_17
  assign out_10[14] = decoder_1_out1 ? 1'b0 : 1'bz;  // Controlled_Buffer controlled_buffer_18
  assign out_10[13] = decoder_1_out1 ? 1'b0 : 1'bz;  // Controlled_Buffer controlled_buffer_19
  assign out_10[12] = decoder_1_out1 ? 1'b0 : 1'bz;  // Controlled_Buffer controlled_buffer_20
  assign out_10[11] = decoder_1_out1 ? _1[11] : 1'bz;  // Controlled_Buffer controlled_buffer_21
  assign out_10[10] = decoder_1_out1 ? _1[10] : 1'bz;  // Controlled_Buffer controlled_buffer_22
  assign out_10[9] = decoder_1_out1 ? _1[9] : 1'bz;  // Controlled_Buffer controlled_buffer_23
  assign out_10[8] = decoder_1_out1 ? _1[8] : 1'bz;  // Controlled_Buffer controlled_buffer_24
  assign out_10[7] = decoder_1_out1 ? _1[7] : 1'bz;  // Controlled_Buffer controlled_buffer_25
  assign out_10[6] = decoder_1_out1 ? _1[6] : 1'bz;  // Controlled_Buffer controlled_buffer_26
  assign out_10[5] = decoder_1_out1 ? _1[5] : 1'bz;  // Controlled_Buffer controlled_buffer_27
  assign out_10[4] = decoder_1_out1 ? _1[4] : 1'bz;  // Controlled_Buffer controlled_buffer_28
  assign out_10[3] = decoder_1_out1 ? _1[3] : 1'bz;  // Controlled_Buffer controlled_buffer_29
  assign out_10[2] = decoder_1_out1 ? _1[2] : 1'bz;  // Controlled_Buffer controlled_buffer_30
  assign out_10[15] = decoder_1_out2 ? 1'b0 : 1'bz;  // Controlled_Buffer controlled_buffer_31
  assign out_10[14] = decoder_1_out2 ? 1'b0 : 1'bz;  // Controlled_Buffer controlled_buffer_32
  assign out_10[1] = decoder_1_out1 ? _1[1] : 1'bz;  // Controlled_Buffer controlled_buffer_33
  assign out_10[0] = decoder_1_out1 ? _1[0] : 1'bz;  // Controlled_Buffer controlled_buffer_34
  assign out_10[13] = decoder_1_out2 ? 1'b0 : 1'bz;  // Controlled_Buffer controlled_buffer_35
  assign out_10[12] = decoder_1_out2 ? 1'b0 : 1'bz;  // Controlled_Buffer controlled_buffer_36
  assign out_10[11] = decoder_1_out2 ? _2[11] : 1'bz;  // Controlled_Buffer controlled_buffer_37
  assign out_10[10] = decoder_1_out2 ? _2[10] : 1'bz;  // Controlled_Buffer controlled_buffer_38
  assign out_10[9] = decoder_1_out2 ? _2[9] : 1'bz;  // Controlled_Buffer controlled_buffer_39
  assign out_10[8] = decoder_1_out2 ? _2[8] : 1'bz;  // Controlled_Buffer controlled_buffer_40
  assign out_10[7] = decoder_1_out2 ? _2[7] : 1'bz;  // Controlled_Buffer controlled_buffer_41
  assign out_10[6] = decoder_1_out2 ? _2[6] : 1'bz;  // Controlled_Buffer controlled_buffer_42
  assign out_10[5] = decoder_1_out2 ? _2[5] : 1'bz;  // Controlled_Buffer controlled_buffer_43
  assign out_10[4] = decoder_1_out2 ? _2[4] : 1'bz;  // Controlled_Buffer controlled_buffer_44
  assign out_10[3] = decoder_1_out2 ? _2[3] : 1'bz;  // Controlled_Buffer controlled_buffer_45
  assign out_10[2] = decoder_1_out2 ? _2[2] : 1'bz;  // Controlled_Buffer controlled_buffer_46
  assign out_10[1] = decoder_1_out2 ? _2[1] : 1'bz;  // Controlled_Buffer controlled_buffer_47
  assign out_10[0] = decoder_1_out2 ? _2[0] : 1'bz;  // Controlled_Buffer controlled_buffer_48
  assign out_10[15] = decoder_1_out3 ? _3[15] : 1'bz;  // Controlled_Buffer controlled_buffer_49
  assign out_10[14] = decoder_1_out3 ? _3[14] : 1'bz;  // Controlled_Buffer controlled_buffer_50
  assign out_10[13] = decoder_1_out3 ? _3[13] : 1'bz;  // Controlled_Buffer controlled_buffer_51
  assign out_10[12] = decoder_1_out3 ? _3[12] : 1'bz;  // Controlled_Buffer controlled_buffer_52
  assign out_10[11] = decoder_1_out3 ? _3[11] : 1'bz;  // Controlled_Buffer controlled_buffer_53
  assign out_10[10] = decoder_1_out3 ? _3[10] : 1'bz;  // Controlled_Buffer controlled_buffer_54
  assign out_10[9] = decoder_1_out3 ? _3[9] : 1'bz;  // Controlled_Buffer controlled_buffer_55
  assign out_10[8] = decoder_1_out3 ? _3[8] : 1'bz;  // Controlled_Buffer controlled_buffer_56
  assign out_10[7] = decoder_1_out3 ? _3[7] : 1'bz;  // Controlled_Buffer controlled_buffer_57
  assign out_10[6] = decoder_1_out3 ? _3[6] : 1'bz;  // Controlled_Buffer controlled_buffer_58
  assign out_10[5] = decoder_1_out3 ? _3[5] : 1'bz;  // Controlled_Buffer controlled_buffer_59
  assign out_10[4] = decoder_1_out3 ? _3[4] : 1'bz;  // Controlled_Buffer controlled_buffer_60
  assign out_10[3] = decoder_1_out3 ? _3[3] : 1'bz;  // Controlled_Buffer controlled_buffer_61
  assign out_10[2] = decoder_1_out3 ? _3[2] : 1'bz;  // Controlled_Buffer controlled_buffer_62
  assign out_10[15] = decoder_1_out4 ? _4[15] : 1'bz;  // Controlled_Buffer controlled_buffer_63
  assign out_10[14] = decoder_1_out4 ? _4[14] : 1'bz;  // Controlled_Buffer controlled_buffer_64
  assign out_10[1] = decoder_1_out3 ? _3[1] : 1'bz;  // Controlled_Buffer controlled_buffer_65
  assign out_10[0] = decoder_1_out3 ? _3[0] : 1'bz;  // Controlled_Buffer controlled_buffer_66
  assign out_10[13] = decoder_1_out4 ? _4[13] : 1'bz;  // Controlled_Buffer controlled_buffer_67
  assign out_10[12] = decoder_1_out4 ? _4[12] : 1'bz;  // Controlled_Buffer controlled_buffer_68
  assign out_10[11] = decoder_1_out4 ? _4[11] : 1'bz;  // Controlled_Buffer controlled_buffer_69
  assign out_10[10] = decoder_1_out4 ? _4[10] : 1'bz;  // Controlled_Buffer controlled_buffer_70
  assign out_10[9] = decoder_1_out4 ? _4[9] : 1'bz;  // Controlled_Buffer controlled_buffer_71
  assign out_10[8] = decoder_1_out4 ? _4[8] : 1'bz;  // Controlled_Buffer controlled_buffer_72
  assign out_10[7] = decoder_1_out4 ? _4[7] : 1'bz;  // Controlled_Buffer controlled_buffer_73
  assign out_10[6] = decoder_1_out4 ? _4[6] : 1'bz;  // Controlled_Buffer controlled_buffer_74
  assign out_10[5] = decoder_1_out4 ? _4[5] : 1'bz;  // Controlled_Buffer controlled_buffer_75
  assign out_10[4] = decoder_1_out4 ? _4[4] : 1'bz;  // Controlled_Buffer controlled_buffer_76
  assign out_10[3] = decoder_1_out4 ? _4[3] : 1'bz;  // Controlled_Buffer controlled_buffer_77
  assign out_10[2] = decoder_1_out4 ? _4[2] : 1'bz;  // Controlled_Buffer controlled_buffer_78
  assign out_10[1] = decoder_1_out4 ? _4[1] : 1'bz;  // Controlled_Buffer controlled_buffer_79
  assign out_10[0] = decoder_1_out4 ? _4[0] : 1'bz;  // Controlled_Buffer controlled_buffer_80
  assign out_10[15] = decoder_1_out5 ? _5[15] : 1'bz;  // Controlled_Buffer controlled_buffer_81
  assign out_10[14] = decoder_1_out5 ? _5[14] : 1'bz;  // Controlled_Buffer controlled_buffer_82
  assign out_10[13] = decoder_1_out5 ? _5[13] : 1'bz;  // Controlled_Buffer controlled_buffer_83
  assign out_10[12] = decoder_1_out5 ? _5[12] : 1'bz;  // Controlled_Buffer controlled_buffer_84
  assign out_10[11] = decoder_1_out5 ? _5[11] : 1'bz;  // Controlled_Buffer controlled_buffer_85
  assign out_10[10] = decoder_1_out5 ? _5[10] : 1'bz;  // Controlled_Buffer controlled_buffer_86
  assign out_10[9] = decoder_1_out5 ? _5[9] : 1'bz;  // Controlled_Buffer controlled_buffer_87
  assign out_10[8] = decoder_1_out5 ? _5[8] : 1'bz;  // Controlled_Buffer controlled_buffer_88
  assign out_10[7] = decoder_1_out5 ? _5[7] : 1'bz;  // Controlled_Buffer controlled_buffer_89
  assign out_10[6] = decoder_1_out5 ? _5[6] : 1'bz;  // Controlled_Buffer controlled_buffer_90
  assign out_10[5] = decoder_1_out5 ? _5[5] : 1'bz;  // Controlled_Buffer controlled_buffer_91
  assign out_10[4] = decoder_1_out5 ? _5[4] : 1'bz;  // Controlled_Buffer controlled_buffer_92
  assign out_10[3] = decoder_1_out5 ? _5[3] : 1'bz;  // Controlled_Buffer controlled_buffer_93
  assign out_10[2] = decoder_1_out5 ? _5[2] : 1'bz;  // Controlled_Buffer controlled_buffer_94
  assign out_10[15] = decoder_1_out6 ? _6[15] : 1'bz;  // Controlled_Buffer controlled_buffer_95
  assign out_10[14] = decoder_1_out6 ? _6[14] : 1'bz;  // Controlled_Buffer controlled_buffer_96
  assign out_10[1] = decoder_1_out5 ? _5[1] : 1'bz;  // Controlled_Buffer controlled_buffer_97
  assign out_10[0] = decoder_1_out5 ? _5[0] : 1'bz;  // Controlled_Buffer controlled_buffer_98
  assign out_10[13] = decoder_1_out6 ? _6[13] : 1'bz;  // Controlled_Buffer controlled_buffer_99
  assign out_10[12] = decoder_1_out6 ? _6[12] : 1'bz;  // Controlled_Buffer controlled_buffer_100
  assign out_10[11] = decoder_1_out6 ? _6[11] : 1'bz;  // Controlled_Buffer controlled_buffer_101
  assign out_10[10] = decoder_1_out6 ? _6[10] : 1'bz;  // Controlled_Buffer controlled_buffer_102
  assign out_10[9] = decoder_1_out6 ? _6[9] : 1'bz;  // Controlled_Buffer controlled_buffer_103
  assign out_10[8] = decoder_1_out6 ? _6[8] : 1'bz;  // Controlled_Buffer controlled_buffer_104
  assign out_10[7] = decoder_1_out6 ? _6[7] : 1'bz;  // Controlled_Buffer controlled_buffer_105
  assign out_10[6] = decoder_1_out6 ? _6[6] : 1'bz;  // Controlled_Buffer controlled_buffer_106
  assign out_10[5] = decoder_1_out6 ? _6[5] : 1'bz;  // Controlled_Buffer controlled_buffer_107
  assign out_10[4] = decoder_1_out6 ? _6[4] : 1'bz;  // Controlled_Buffer controlled_buffer_108
  assign out_10[3] = decoder_1_out6 ? _6[3] : 1'bz;  // Controlled_Buffer controlled_buffer_109
  assign out_10[2] = decoder_1_out6 ? _6[2] : 1'bz;  // Controlled_Buffer controlled_buffer_110
  assign out_10[1] = decoder_1_out6 ? _6[1] : 1'bz;  // Controlled_Buffer controlled_buffer_111
  assign out_10[0] = decoder_1_out6 ? _6[0] : 1'bz;  // Controlled_Buffer controlled_buffer_112
  assign out_10[15] = decoder_1_out7 ? _7[15] : 1'bz;  // Controlled_Buffer controlled_buffer_113
  assign out_10[14] = decoder_1_out7 ? _7[14] : 1'bz;  // Controlled_Buffer controlled_buffer_114
  assign out_10[13] = decoder_1_out7 ? _7[13] : 1'bz;  // Controlled_Buffer controlled_buffer_115
  assign out_10[12] = decoder_1_out7 ? _7[12] : 1'bz;  // Controlled_Buffer controlled_buffer_116
  assign out_10[11] = decoder_1_out7 ? _7[11] : 1'bz;  // Controlled_Buffer controlled_buffer_117
  assign out_10[10] = decoder_1_out7 ? _7[10] : 1'bz;  // Controlled_Buffer controlled_buffer_118
  assign out_10[9] = decoder_1_out7 ? _7[9] : 1'bz;  // Controlled_Buffer controlled_buffer_119
  assign out_10[8] = decoder_1_out7 ? _7[8] : 1'bz;  // Controlled_Buffer controlled_buffer_120
  assign out_10[7] = decoder_1_out7 ? _7[7] : 1'bz;  // Controlled_Buffer controlled_buffer_121
  assign out_10[6] = decoder_1_out7 ? _7[6] : 1'bz;  // Controlled_Buffer controlled_buffer_122
  assign out_10[5] = decoder_1_out7 ? _7[5] : 1'bz;  // Controlled_Buffer controlled_buffer_123
  assign out_10[4] = decoder_1_out7 ? _7[4] : 1'bz;  // Controlled_Buffer controlled_buffer_124
  assign out_10[3] = decoder_1_out7 ? _7[3] : 1'bz;  // Controlled_Buffer controlled_buffer_125
  assign out_10[2] = decoder_1_out7 ? _7[2] : 1'bz;  // Controlled_Buffer controlled_buffer_126
  assign out_10[1] = decoder_1_out7 ? _7[1] : 1'bz;  // Controlled_Buffer controlled_buffer_127
  assign out_10[0] = decoder_1_out7 ? _7[0] : 1'bz;  // Controlled_Buffer controlled_buffer_128
endmodule

module control (
  input  CLK,
  input  [15:0] IR,
  input  [15:0] DR,
  input  [15:0] AC,
  input  fgi,
  input  fgo,
  input  E_in,
  output LD,
  output AR,
  output out_10,
  output LD_2,
  output INR,
  output CLR,
  output LD_3,
  output INR_2,
  output [3:0] alu_sel,
  output LD_4,
  output INR_3,
  output CLR_2,
  output [2:0] bus1_out,
  output TR,
  output IR_2,
  output inp,
  output out,
  output mem_red,
  output mem_write
);

  wire add_out, and_1_out, and_2_out, and_3_out, and_4_out, and_5_out, and_6_out, and_7_out, and_8_out,
       and_9_out, and_10_out, and_11_out, and_12_out, and_13_out, and_14_out, and_15_out, and_18_out,
       and_19_out, and_20_out, and_21_out, and_23_out, and_24_out, and_25_out, and_28_out, and_29_out,
       and_30_out, and_33_out, and_34_out, and_35_out, and_38_out, and_39_out, and_40_out, and_41_out,
       and_42_out, and_43_out, and_44_out, and_46_out, and_47_out, and_50_out, and_51_out, and_52_out,
       and_53_out, and_56_out, cil_out, cir_out, com_out, d_ff_1_q, d_ff_2_q, decoder_1_out0, decoder_1_out1,
       decoder_1_out2, decoder_1_out3, decoder_1_out4, decoder_1_out5, decoder_1_out6, decoder_1_out7,
       decoder_1_out8, decoder_1_out9, decoder_1_out10, decoder_1_out11, decoder_1_out12, decoder_1_out13,
       decoder_1_out14, decoder_1_out15, decoder_2_out0, decoder_2_out1, decoder_2_out2, decoder_2_out3,
       decoder_2_out4, decoder_2_out5, decoder_2_out6, decoder_2_out7, E_q, E_qn, I_q, I_qn, if_2_out,
       if_3_out, if_4_out, if_5_out, if_6_out, if_7_out, if_out, j_k_ff_1_q, j_k_ff_2_q, j_k_ff_3_q,
       not_1_out, not_2_out, not_3_out, not_4_out, not_5_out, not_6_out, not_7_out, not_8_out, not_9_out,
       not_10_out, not_11_out, or_1_out, or_2_out, or_3_out, or_4_out, or_5_out, or_6_out, or_7_out,
       or_9_out, or_10_out, or_11_out, or_15_out, or_16_out, or_18_out, or_23_out, p_out, R_2_q, r_out, S_q,
       SC_CLR_out;
  wire [2:0] priority_encoder_1_out;
  wire [3:0] nor_1_out, nor_2_out, undriven;
  wire [7:0] SC_out;
  wire [7:1] or_20_out;

  not not_1 (not_1_out, SC_CLR_out);
  Decoder #(.select(4)) decoder_1 (
    .out0(decoder_1_out0), .out1(decoder_1_out1), .out2(decoder_1_out2), .out3(decoder_1_out3),
    .out4(decoder_1_out4), .out5(decoder_1_out5), .out6(decoder_1_out6), .out7(decoder_1_out7),
    .out8(decoder_1_out8), .out9(decoder_1_out9), .out10(decoder_1_out10), .out11(decoder_1_out11),
    .out12(decoder_1_out12), .out13(decoder_1_out13), .out14(decoder_1_out14), .out15(decoder_1_out15),
    .sel(SC_out[3:0]));  // open: en
  not not_2 (not_2_out, CLK);
  _8bit_register SC (.clk(CLK), .\input ({8{1'b0}}), .out(SC_out), .ld(1'b0), .inc(not_1_out), .clr(SC_CLR_out));
  // Probe on SC_out[3:0]
  or or_1 (or_1_out, decoder_1_out5, decoder_1_out4);
  D_Flip_Flop d_ff_1 (.clk(CLK), .D(CLK), .Q(d_ff_1_q));  // open: Qn, preset, en, reset
  D_Flip_Flop d_ff_2 (.clk(not_2_out), .D(d_ff_1_q), .Q(d_ff_2_q));  // open: Qn, preset, en, reset
  Decoder #(.select(3)) decoder_2 (
    .out0(decoder_2_out0), .out1(decoder_2_out1), .out2(decoder_2_out2), .out3(decoder_2_out3),
    .out4(decoder_2_out4), .out5(decoder_2_out5), .out6(decoder_2_out6), .out7(decoder_2_out7),
    .sel(IR[14:12]));  // open: en
  and and_1 (and_1_out, d_ff_2_q, CLK);
  // Probe on IR
  and and_2 (and_2_out, decoder_1_out2, not_9_out);
  D_Flip_Flop I (.clk(and_2_out), .D(IR[15]), .Q(I_q), .Qn(I_qn));  // open: preset, en, reset
  or or_2 (or_2_out, decoder_1_out3, decoder_1_out4);
  and r (r_out, I_qn, decoder_2_out7, decoder_1_out3);
  and p (p_out, I_q, decoder_2_out7, decoder_1_out3);
  or or_3 (or_3_out, decoder_2_out3, decoder_2_out4);
  not not_3 (not_3_out, decoder_2_out7);
  or or_4 (or_4_out, decoder_2_out0, decoder_2_out1, decoder_2_out2, decoder_2_out5);
  and and_3 (and_3_out, or_3_out, decoder_1_out4);
  and and_4 (and_4_out, decoder_2_out6, decoder_1_out6);
  and and_5 (and_5_out, decoder_1_out2, R_2_q);
  and and_6 (and_6_out, I_q, not_3_out, decoder_1_out3);
  or or_5 (or_5_out, decoder_1_out4, decoder_1_out5);
  not not_4 (not_4_out, decoder_1_out0);
  not not_5 (not_5_out, decoder_1_out1);
  not not_6 (not_6_out, decoder_1_out2);
  and and_7 (and_7_out, decoder_1_out5, or_4_out);
  or or_6 (or_6_out, decoder_2_out0, decoder_2_out1, decoder_2_out2, decoder_2_out6);
  not not_7 (not_7_out, R_2_q);
  and and_8 (and_8_out, R_2_q, decoder_1_out1);
  or or_7 (or_7_out, decoder_2_out3, decoder_2_out5);
  and and_9 (and_9_out, or_7_out, decoder_1_out4);
  and and_10 (and_10_out, decoder_2_out6, decoder_1_out6);
  not not_8 (not_8_out, decoder_2_out7);
  not not_9 (not_9_out, R_2_q);
  not not_10 (not_10_out, R_2_q);
  and and_11 (and_11_out, or_6_out, or_1_out);
  and and_12 (and_12_out, decoder_1_out1, not_7_out);
  and and_13 (and_13_out, not_8_out, I_q, or_2_out);
  and and_14 (and_14_out, decoder_1_out2, not_9_out);
  and and_15 (and_15_out, not_9_out, decoder_1_out0);
  and and_16 (AR, decoder_2_out5, decoder_1_out4);
  and and_17 (out_10, decoder_1_out0, R_2_q);
  and and_18 (and_18_out, decoder_2_out4, decoder_1_out4);
  and and_19 (and_19_out, decoder_2_out5, decoder_1_out5);
  and and_20 (and_20_out, not_9_out, decoder_1_out1);
  and and_21 (and_21_out, R_2_q, decoder_1_out2);
  and \if  (if_out, decoder_2_out6, and_52_out, decoder_1_out6);
  and if_2 (if_2_out, r_out, E_qn, IR[1]);
  and if_3 (if_3_out, r_out, and_56_out, IR[2]);
  and if_4 (if_4_out, r_out, AC[15], IR[3]);
  and if_5 (if_5_out, r_out, not_11_out, IR[4]);
  and if_6 (if_6_out, p_out, j_k_ff_3_q, IR[8]);
  and if_7 (if_7_out, p_out, j_k_ff_2_q, IR[9]);
  and and_22 (CLR, R_2_q, decoder_1_out1);
  or or_8 (LD_2, and_18_out, and_19_out);
  or or_9 (or_9_out, and_20_out, and_21_out, if_out);
  or or_10 (or_10_out, if_2_out, if_3_out, if_4_out);
  or or_11 (or_11_out, if_5_out, if_6_out, if_7_out);
  or SC_CLR (SC_CLR_out, and_7_out, and_3_out, and_4_out, and_5_out, r_out, p_out);
  or or_12 (mem_red, and_11_out, and_12_out, and_6_out);
  or or_13 (mem_write, and_8_out, and_9_out, and_10_out);
  or or_14 (LD, and_13_out, and_14_out, and_15_out);
  or or_15 (or_15_out, decoder_2_out0, decoder_2_out1, decoder_2_out2, decoder_2_out6);
  and and_23 (and_23_out, decoder_2_out0, decoder_1_out5);
  and add (add_out, decoder_2_out1, decoder_1_out5);
  and and_24 (and_24_out, decoder_2_out2, decoder_1_out5);
  and and_25 (and_25_out, p_out, IR[11]);
  and com (com_out, r_out, IR[9]);
  and cir (cir_out, r_out, IR[7]);
  and cil (cil_out, r_out, IR[6]);
  and and_26 (INR_3, r_out, IR[5]);
  and and_27 (CLR_2, r_out, IR[11]);
  and and_28 (and_28_out, not_4_out, not_5_out, j_k_ff_1_q, not_6_out);
  or or_16 (or_16_out, j_k_ff_2_q, j_k_ff_3_q);
  and and_29 (and_29_out, r_out, IR[8]);
  and and_30 (and_30_out, r_out, IR[10]);
  or or_17 (INR, or_9_out, or_10_out, or_11_out);
  not not_11 (not_11_out, AC[15]);
  and and_31 (LD_3, or_15_out, decoder_1_out4);
  and and_32 (INR_2, decoder_1_out5, decoder_2_out6);
  and and_33 (and_33_out, p_out, IR[7]);
  and and_34 (and_34_out, p_out, IR[6]);
  and and_35 (and_35_out, decoder_1_out2, R_2_q);
  and and_36 (inp, p_out, IR[11]);
  and and_37 (out, IR[10], p_out);
  and and_38 (and_38_out, and_28_out, or_16_out);
  and and_39 (and_39_out, r_out, IR[0]);
  and and_40 (and_40_out, decoder_1_out4, decoder_2_out4);
  and and_41 (and_41_out, decoder_1_out5, decoder_2_out5);
  and and_42 (and_42_out, not_10_out, decoder_1_out0);
  and and_43 (and_43_out, R_2_q, decoder_1_out0);
  and and_44 (and_44_out, decoder_2_out5, decoder_1_out4);
  and and_45 (or_20_out[3], decoder_1_out6, decoder_2_out6);
  and and_46 (and_46_out, decoder_2_out3, decoder_1_out4);
  and and_47 (and_47_out, p_out, IR[10]);
  and and_48 (or_20_out[5], not_10_out, decoder_1_out2);
  and and_49 (or_20_out[6], R_2_q, decoder_1_out1);
  and and_50 (and_50_out, not_10_out, decoder_1_out1);
  and and_51 (and_51_out, decoder_2_out7, decoder_1_out3, I_q);
  or or_18 (or_18_out, and_34_out, and_35_out);
  assign nor_1_out = ~(DR[15:12] | DR[11:8] | DR[7:4] | DR[3:0]);  // NOR_Gate nor_1, 4 bits wide
  and and_52 (and_52_out, nor_1_out[3], nor_1_out[2], nor_1_out[1], nor_1_out[0]);
  or or_19 (LD_4, and_23_out, add_out, and_24_out, and_25_out, com_out, cir_out, cil_out);
  Priority_Encoder priority_encoder_1 (
    .in0(and_23_out), .in1(add_out), .in2(com_out), .in3(cir_out), .in4(cil_out), .in5(1'b0), .in6(1'b0),
    .in7(1'b0), .out(priority_encoder_1_out));  // open: en_in, gs, en_out
  or or_20 (or_20_out[1], and_40_out, and_41_out);
  or or_21 (or_20_out[2], and_42_out, and_43_out, 1'b0, and_44_out);
  or or_22 (or_20_out[4], and_46_out, and_47_out);
  or or_23 (or_23_out, decoder_2_out0, decoder_2_out1, decoder_2_out2, decoder_2_out6);
  J_K_Flip_Flop R_2 (.J(and_38_out), .clk(CLK), .Q(R_2_q));  // open: K, Qn, preset, en, reset
  J_K_Flip_Flop E (
    .J(and_29_out), .clk(CLK), .K(and_29_out), .Q(E_q), .Qn(E_qn), .preset(E_in), .reset(and_30_out));  // open: en
  J_K_Flip_Flop S (.clk(CLK), .Q(S_q), .reset(and_39_out));  // open: J, K, Qn, preset, en
  or or_24 (or_20_out[7], and_50_out, and_51_out, and_53_out);
  and and_53 (and_53_out, or_23_out, or_5_out);
  and and_54 (TR, decoder_1_out0, R_2_q);
  and and_55 (IR_2, not_10_out, decoder_1_out1);
  J_K_Flip_Flop j_k_ff_1 (.J(and_33_out), .clk(CLK), .K(or_18_out), .Q(j_k_ff_1_q));  // open: Qn, preset, en, reset
  J_K_Flip_Flop j_k_ff_2 (.J(fgi), .clk(CLK), .K(inp), .Q(j_k_ff_2_q));  // open: Qn, preset, en, reset
  J_K_Flip_Flop j_k_ff_3 (.J(fgo), .clk(CLK), .K(out), .Q(j_k_ff_3_q));  // open: Qn, preset, en, reset
  assign nor_2_out = ~(AC[15:12] | AC[11:8] | AC[7:4] | AC[3:0]);  // NOR_Gate nor_2, 4 bits wide
  and and_56 (and_56_out, nor_2_out[3], nor_2_out[2], nor_2_out[1], nor_2_out[0]);
  Multiplexer #(.select(3), .width(4), .disabled(0), .enable("false")) multiplexer_1 (
    .in0(4'b0100), .in1(4'b0000), .in2(4'b0111), .in3(4'b1101), .in4(4'b1000), .in5(undriven),
    .in6(undriven), .in7(undriven), .out(alu_sel), .sel(priority_encoder_1_out));
  Priority_Encoder #(.disabled(0)) priority_encoder_2 (
    .in0(1'b0), .in1(or_20_out[1]), .in2(or_20_out[2]), .in3(or_20_out[3]), .in4(or_20_out[4]),
    .in5(or_20_out[5]), .in6(or_20_out[6]), .in7(or_20_out[7]), .out(bus1_out), .en_in(1'b1));  // open: gs, en_out

  // Notes on the sheet:
  //   R'
  //   I
  //   FGI
  //   FGO
  //   E'
  //   R
  //   R
  //   INR
  //   CLR
  //   DR=0
  //   AC=0
  //   AC15=1
  //   AC15=0
  //   R'
  //   R
  //   p
  //   R'
  //   R
  //   R'
  //   I
  //   PC
  //   x6
  //   R'
  //   CLR
  //   CLR
  //   DR
  //   AC
  //   x1
  //   x3
  //   x4
  //   x5
  //   x2
  //   x7
  //   IEN
  //   LD
  //   LD
  //   FGI
  //   FGO
  //   BUS1
endmodule

module simple_comp_w_control (
  input  [11:0] in_1,
  input  [7:0] \input ,
  input  FGI,
  input  FGI_2,
  output [7:0] \output 
);

  wire button_1_out, clock_1_out, control_1_ar, control_1_clr, control_1_clr_2, control_1_inp, control_1_inr,
       control_1_inr_2, control_1_inr_3, control_1_ir_2, control_1_ld, control_1_ld_2, control_1_ld_3,
       control_1_ld_4, control_1_mem_red, control_1_mem_write, control_1_out, control_1_out_10, control_1_tr,
       n16bit_alu_1_c_out, not_1_out, or_1_out;
  wire [2:0] control_1_bus1_out;
  wire [3:0] AC_out, AC_out_2, AC_out_4, control_1_alu_sel;
  wire [7:0] INPR_out;
  wire [11:0] AR_out, controlled_buffer_1_out, n12bit_register_1_out, n12bit_register_2_out;
  wire [11:8] AC_out_3;
  wire [15:0] alu_ac_inprselect_1_out16bit, bus1_1_out_10, controlled_buffer_2_out, controlled_buffer_3_out,
       DR_out, IR_out, n16bit_alu_1_out, TR_out;

  // Probe on in_1
  Clock clock_1 (.out(clock_1_out));
  Button button_1 (.out(button_1_out));
  // Probe on n12bit_register_1_out
  _12bit_register u_12bit_register_1 (
    .clk(button_1_out), .\input (in_1), .out(n12bit_register_1_out), .ld(1'b1));  // open: inc, clr
  control control_1 (
    .LD(control_1_ld), .AR(control_1_ar), .out_10(control_1_out_10), .LD_2(control_1_ld_2),
    .INR(control_1_inr), .CLR(control_1_clr), .LD_3(control_1_ld_3), .INR_2(control_1_inr_2),
    .LD_4(control_1_ld_4), .INR_3(control_1_inr_3), .CLR_2(control_1_clr_2), .TR(control_1_tr),
    .IR_2(control_1_ir_2), .IR(IR_out), .DR(DR_out), .AC({AC_out_4, AC_out_3, AC_out_2, AC_out}),
    .bus1_out(control_1_bus1_out), .fgi(FGI), .fgo(FGI_2), .E_in(n16bit_alu_1_c_out), .CLK(clock_1_out),
    .mem_red(control_1_mem_red), .mem_write(control_1_mem_write), .inp(control_1_inp), .out(control_1_out),
    .alu_sel(control_1_alu_sel));
  assign controlled_buffer_1_out = or_1_out ? AR_out : 12'bz;  // Controlled_Buffer controlled_buffer_1
  or or_1 (or_1_out, control_1_mem_red, control_1_mem_write);
  // Probe on AR_out
  _12bit_register AR (
    .clk(clock_1_out), .\input (bus1_1_out_10[11:0]), .out(AR_out), .ld(control_1_ld), .inc(control_1_ar),
    .clr(control_1_out_10));
  bus1 bus1_1 (
    .in_9(control_1_bus1_out), .out_10(bus1_1_out_10), ._1(AR_out), ._2(n12bit_register_2_out), ._3(DR_out),
    ._4({AC_out_4, AC_out_3, AC_out_2, AC_out}), ._5(IR_out), ._6(TR_out), ._7(controlled_buffer_3_out));  // open: _0
  assign controlled_buffer_2_out = not_1_out ? bus1_1_out_10 : 16'bz;  // Controlled_Buffer controlled_buffer_2
  RAM #(.addrWidth(12), .dataWidth(16)) ram_1 (
    .addr(controlled_buffer_1_out), .data(controlled_buffer_2_out), .sel(or_1_out), .clk(clock_1_out),
    .ld(control_1_mem_red));  // open: clr
  not not_1 (not_1_out, control_1_mem_red);
  // Probe on control_1_bus1_out
  assign controlled_buffer_3_out = control_1_mem_red ? controlled_buffer_2_out : 16'bz;  // Controlled_Buffer controlled_buffer_3
  // Probe on n12bit_register_2_out
  _12bit_register u_12bit_register_2 (
    .clk(clock_1_out), .\input (bus1_1_out_10[11:0]), .out(n12bit_register_2_out), .ld(control_1_ld_2),
    .inc(control_1_inr), .clr(control_1_clr));
  // Probe on DR_out
  _16bit_register DR (
    .clk(clock_1_out), .\input (bus1_1_out_10), .out(DR_out), .ld(control_1_ld_3), .inc(control_1_inr_2));  // open: clr
  _8bit_register INPR (.clk(clock_1_out), .\input (\input ), .out(INPR_out), .ld(control_1_inp));  // open: inc, clr
  alu_ac_inprSelect alu_ac_inprselect_1 (
    .in16bit({AC_out_4, AC_out_3, AC_out_2, AC_out}), .in8bit(INPR_out), ._16_8_select(control_1_inp),
    .out16bit(alu_ac_inprselect_1_out16bit));
  _8bit_register OUTR (
    .clk(clock_1_out), .\input (bus1_1_out_10[7:0]), .out(\output ), .ld(control_1_out));  // open: inc, clr
  _16bit_alu u_16bit_alu_1 (
    .out(n16bit_alu_1_out), .c_out(n16bit_alu_1_c_out), .a(DR_out), .b(alu_ac_inprselect_1_out16bit),
    .s(control_1_alu_sel), .c_in(1'b0));
  Hex_Digit_Display hex_digit_display_1 (.value(bus1_1_out_10[15:12]));  // open: dp
  Hex_Digit_Display hex_digit_display_2 (.value(bus1_1_out_10[11:8]));  // open: dp
  Hex_Digit_Display hex_digit_display_3 (.value(AC_out_4));  // open: dp
  _16bit_register AC (
    .clk(clock_1_out), .\input (n16bit_alu_1_out), .out({AC_out_4, AC_out_3, AC_out_2, AC_out}),
    .ld(control_1_ld_4), .inc(control_1_inr_3), .clr(control_1_clr_2));
  Hex_Digit_Display hex_digit_display_4 (.value(bus1_1_out_10[3:0]));  // open: dp
  Hex_Digit_Display hex_digit_display_5 (.value(bus1_1_out_10[7:4]));  // open: dp
  Hex_Digit_Display hex_digit_display_6 (.value(AC_out_2));  // open: dp
  Hex_Digit_Display hex_digit_display_7 (.value(AC_out_3));  // open: dp
  Hex_Digit_Display hex_digit_display_8 (.value(AC_out));  // open: dp
  // Probe on IR_out
  _16bit_register IR (.clk(clock_1_out), .\input (bus1_1_out_10), .out(IR_out), .ld(control_1_ir_2));  // open: inc, clr
  _16bit_register TR (.clk(clock_1_out), .\input (bus1_1_out_10), .out(TR_out), .ld(control_1_tr));  // open: inc, clr
  // Probe on TR_out

  // Notes on the sheet:
  //   7
  //   1
  //   PC
  //   s
  //   2
  //   3
  //   4
  //   5
  //   6
endmodule

module mapping_microprg (
  input  [15:0] IR,
  output [7:0] map,
  output indrt
);

  wire and_1_out, undriven;
  wire [1:0] multiplexer_1_out, multiplexer_2_out;
  wire [3:0] priority_encoder_1_out;

  // Probe on IR
  Priority_Encoder #(.select(4)) priority_encoder_1 (
    .in0(IR[0]), .in1(IR[1]), .in2(IR[2]), .in3(IR[3]), .in4(IR[4]), .in5(IR[5]), .in6(IR[6]), .in7(IR[7]),
    .in8(IR[8]), .in9(IR[9]), .in10(IR[10]), .in11(IR[11]), .in12(1'b0), .in13(1'b0), .in14(1'b0),
    .in15(1'b0), .out(priority_encoder_1_out), .en_in(undriven));  // open: gs, en_out
  Multiplexer #(.width(2)) multiplexer_1 (.in0(2'b01), .in1(2'b10), .out(multiplexer_1_out), .sel(IR[15]));  // open: en
  Multiplexer #(.width(2)) multiplexer_2 (
    .in0(2'b00), .in1(multiplexer_1_out), .out(multiplexer_2_out), .sel(IR[12]));  // open: en
  Multiplexer #(.width(8)) multiplexer_3 (
    .in0({3'b000, IR[14:12], 2'b00}), .in1({multiplexer_2_out, priority_encoder_1_out, 2'b00}), .out(map),
    .sel(and_1_out));  // open: en
  and and_1 (and_1_out, IR[12], IR[13], IR[14]);
  // Probe on map

  assign indrt = IR[15];

  // Notes on the sheet:
  //   mem ref
  //   reg-ref/io
endmodule

module microprg_contrl (
  input  [15:0] DR,
  input  [15:0] AC,
  input  [15:0] IR,
  input  clk,
  input  E,
  input  fgi,
  input  fgo,
  output [3:0] out_8,
  output [2:0] bus1_out,
  output out_10,
  output INCAC,
  output LDAC,
  output out_13,
  output LDDR,
  output out_15,
  output out_16,
  output out_17,
  output out_18,
  output out_19,
  output out_20,
  output WRITE,
  output inp_ld,
  output \bus2_sel__ır_ld ,
  output LDIR,
  output CLRAR,
  output out_26,
  output out_27
);

  wire and_1_out, and_2_out, and_3_out, decoder_1_out0, decoder_1_out3, decoder_1_out4, decoder_1_out5,
       decoder_1_out6, decoder_1_out7, decoder_1_out9, decoder_1_out10, decoder_2_out0, decoder_2_out2,
       decoder_2_out3, decoder_2_out4, decoder_2_out7, decoder_2_out8, decoder_2_out9, decoder_2_out11,
       decoder_2_out12, decoder_2_out13, decoder_2_out14, decoder_2_out15, decoder_3_out0, decoder_3_out1,
       decoder_3_out2, decoder_3_out5, fgi_q, fgo_q, ien_q, not_1_out, or_5_out, or_6_out, r_q, s_q,
       undriven, undriven_2, undriven_3, undriven_4;
  wire [2:0] priority_encoder_2_out, sequencer_microprg_1_out_11;
  wire [3:0] nor_1_out, nor_2_out, sequencer_microprg_1_out_9, sequencer_microprg_1_out_10;

  assign nor_1_out = ~(DR[15:12] | DR[11:8] | DR[7:4] | DR[3:0]);  // NOR_Gate nor_1, 4 bits wide
  and and_1 (and_1_out, nor_1_out[3], nor_1_out[2], nor_1_out[1], nor_1_out[0]);
  assign nor_2_out = ~(AC[15:12] | AC[11:8] | AC[7:4] | AC[3:0]);  // NOR_Gate nor_2, 4 bits wide
  and and_2 (and_2_out, nor_2_out[3], nor_2_out[2], nor_2_out[1], nor_2_out[0]);
  Decoder #(.select(4)) decoder_1 (
    .out0(decoder_1_out0), .out1(out_10), .out2(INCAC), .out3(decoder_1_out3), .out4(decoder_1_out4),
    .out5(decoder_1_out5), .out6(decoder_1_out6), .out7(decoder_1_out7), .out8(out_13),
    .out9(decoder_1_out9), .out10(decoder_1_out10), .out11(\bus2_sel__ır_ld ), .out12(out_16),
    .out13(out_17), .out14(out_20), .out15(out_18), .sel(sequencer_microprg_1_out_9));  // open: en
  not not_1 (not_1_out, E);
  Decoder #(.select(4)) decoder_2 (
    .out0(decoder_2_out0), .out1(decoder_1_out3), .out2(decoder_2_out2), .out3(decoder_2_out3),
    .out4(decoder_2_out4), .out5(\bus2_sel__ır_ld ), .out6(inp_ld), .out7(decoder_2_out7),
    .out8(decoder_2_out8), .out9(decoder_2_out9), .out10(out_13), .out11(decoder_2_out11),
    .out12(decoder_2_out12), .out13(decoder_2_out13), .out14(decoder_2_out14), .out15(decoder_2_out15),
    .sel(sequencer_microprg_1_out_10));  // open: en
  sequencer_microprg sequencer_microprg_1 (
    .in_1(IR), .acs(AC[15]), .acz(and_2_out), .ez(not_1_out), .r(r_q), .fg(or_6_out), .drz(and_1_out),
    .clk(clk), .out_11(sequencer_microprg_1_out_11), .out_10(sequencer_microprg_1_out_10),
    .out_9(sequencer_microprg_1_out_9));
  Decoder #(.select(3)) decoder_3 (
    .out0(decoder_3_out0), .out1(decoder_3_out1), .out2(decoder_3_out2), .out3(CLRAR),
    .out4(\bus2_sel__ır_ld ), .out5(decoder_3_out5), .out6(out_19), .out7(out_27),
    .sel(sequencer_microprg_1_out_11));  // open: en
  Priority_Encoder priority_encoder_1 (
    .in0(undriven), .in1(out_19), .in2(out_20), .in3(decoder_1_out3), .in4(out_13), .in5(decoder_3_out5),
    .in6(decoder_2_out2), .in7(\bus2_sel__ır_ld ), .out(bus1_out));  // open: en_in
  Multiplexer #(.select(3), .width(4)) multiplexer_1 (
    .in0(4'b0111), .in1(4'b1101), .in2(4'b1000), .in3(4'b0000), .in4(4'b0100), .out(out_8),
    .sel(priority_encoder_2_out));  // open: in5, in6, in7, en
  Priority_Encoder priority_encoder_2 (
    .in0(decoder_1_out4), .in1(decoder_1_out5), .in2(decoder_1_out6), .in3(decoder_1_out9),
    .in4(decoder_1_out10), .in5(undriven_2), .in6(undriven_3), .in7(undriven_4), .out(priority_encoder_2_out));  // open: en_in
  or or_1 (LDAC, decoder_1_out3, decoder_1_out4, decoder_1_out5, decoder_1_out6, decoder_1_out7, decoder_1_out9, decoder_1_out10);
  or or_2 (WRITE, decoder_1_out3, decoder_2_out2, out_13);
  or or_3 (out_15, \bus2_sel__ır_ld , \bus2_sel__ır_ld , \bus2_sel__ır_ld );
  or or_4 (out_26, \bus2_sel__ır_ld , decoder_3_out5);
  or or_5 (or_5_out, E, decoder_2_out4);
  and and_3 (and_3_out, ien_q, or_6_out);
  J_K_Flip_Flop u_E (.J(or_5_out), .clk(clk), .K(decoder_2_out4), .reset(decoder_2_out3));  // open: Q, Qn, preset, en
  J_K_Flip_Flop u_fgi (.clk(clk), .Q(fgi_q), .preset(fgi), .reset(inp_ld));  // open: J, K, Qn, en
  J_K_Flip_Flop u_fgo (.clk(clk), .Q(fgo_q), .preset(fgo), .reset(decoder_2_out7));  // open: J, K, Qn, en
  J_K_Flip_Flop r (.clk(clk), .Q(r_q), .preset(and_3_out), .reset(decoder_2_out8));  // open: J, K, Qn, en
  J_K_Flip_Flop s (.clk(clk), .Q(s_q), .reset(decoder_2_out9));  // open: J, K, Qn, preset, en
  J_K_Flip_Flop ien (.clk(clk), .Q(ien_q), .preset(decoder_3_out2), .reset(decoder_3_out1));  // open: J, K, Qn, en
  or or_6 (or_6_out, fgo_q, fgi_q);

  assign LDDR = \bus2_sel__ır_ld ;
  assign LDIR = \bus2_sel__ır_ld ;

  // Notes on the sheet:
  //   f1
  //   f2
  //   f3
  //   read
  //   incdr
  //   incpc
  //   pcttr
  //   clrpc
  //   write
  //   write2
  //   come
  //   indr
  //   clfgi
  //   clfgo
  //   clrr
  //   clrs
  //   write3
  //   clrien
  //   setien
  //   clrar
  //   rdins
  //   irtar
  //   artpc
  //   incar
  //   clrac
  //   incac
  //   drtac
  //   comac
  //   cirac
  //   cil-ac
  //   inpt
  //   outpt
  //   add
  //   and
  //   clre
  //   INCDR
  //   CLRPC
  //   LDPC
  //   LDTR
  //   CLRAC
  //   READ
  //   INCPC
  //   LDAR
  //   INCAR
endmodule

module sequencer_microprg (
  input  [15:0] in_1,
  input  clk,
  input  acs,
  input  acz,
  input  ez,
  input  r,
  input  fg,
  input  drz,
  output [3:0] out_9,
  output [3:0] out_10,
  output [2:0] out_11
);

  wire and_1_out, and_2_out, and_3_out, mapping_microprg_1_indrt, multiplexer_1_out, not_1_out;
  wire [0:0] or_1_out;
  wire [1:0] rom_1_data;
  wire [2:0] rom_1_data_2;
  wire [7:0] adder_1_out, CAR_out, mapping_microprg_1_map, multiplexer_2_out, rom_1_data_3, SBR_out;

  and and_1 (and_1_out, rom_1_data[1], rom_1_data[0]);
  Multiplexer #(.select(3), .enable("false")) multiplexer_1 (
    .in0(1'b1), .in1(mapping_microprg_1_indrt), .in2(acs), .in3(acz), .in4(ez), .in5(r), .in6(fg), .in7(drz),
    .out(multiplexer_1_out), .sel(rom_1_data_2));
  not not_1 (not_1_out, rom_1_data[1]);
  and and_2 (and_2_out, not_1_out, multiplexer_1_out);
  and and_3 (and_3_out, not_1_out, rom_1_data[0], multiplexer_1_out);
  or or_1 (or_1_out[0], and_2_out, and_1_out);
  Multiplexer #(.select(2), .width(8), .enable("false")) multiplexer_2 (
    .in0(adder_1_out), .in1(rom_1_data_3), .in2(SBR_out), .in3(mapping_microprg_1_map),
    .out(multiplexer_2_out), .sel({rom_1_data[1], or_1_out[0]}));
  _8bit_register CAR (.clk(clk), .\input (multiplexer_2_out), .out(CAR_out), .ld(1'b1));  // open: inc, clr
  mapping_microprg mapping_microprg_1 (.IR(in_1), .indrt(mapping_microprg_1_indrt), .map(mapping_microprg_1_map));
  Adder adder_1 (.a(CAR_out), .b(8'h1), .out(adder_1_out));  // open: cin, cout
  ROM #(.dataWidth(24)) rom_1 (
    .addr(CAR_out), .data({out_9, out_10, out_11, rom_1_data_2, rom_1_data, rom_1_data_3}));  // open: sel
  _8bit_register SBR (.clk(clk), .\input (adder_1_out), .out(SBR_out), .ld(and_3_out));  // open: inc, clr

  // Notes on the sheet:
  //   indr
  //   T
  //   mapp
  //   contents of rom_1 (hex, n*v repeats v):
  //   d00001
  //   F1
  //   F2
  //   F3
  //   CD
  //   BR
  //   AD
endmodule

module comp_w_microprg_contr (
  input  [11:0] in_1,
  input  [7:0] \input ,
  input  FGI,
  input  FGO,
  output [7:0] \output 
);

  wire button_1_out, clock_1_out, \microprg_contrl_1_bus2_sel__ır_ld , microprg_contrl_1_clrar,
       microprg_contrl_1_incac, microprg_contrl_1_inp_ld, microprg_contrl_1_ldac, microprg_contrl_1_lddr,
       microprg_contrl_1_ldir, microprg_contrl_1_out_10, microprg_contrl_1_out_13, microprg_contrl_1_out_15,
       microprg_contrl_1_out_16, microprg_contrl_1_out_17, microprg_contrl_1_out_18,
       microprg_contrl_1_out_19, microprg_contrl_1_out_20, microprg_contrl_1_out_26,
       microprg_contrl_1_out_27, microprg_contrl_1_write, n16bit_alu_1_c_out, not_1_out, or_1_out;
  wire [2:0] microprg_contrl_1_bus1_out;
  wire [3:0] AC_out, AC_out_2, AC_out_4, microprg_contrl_1_out_8;
  wire [7:0] INPR_out;
  wire [11:0] AR_out, ar_pc_bus2_1_out, controlled_buffer_1_out, n12bit_register_1_out, n12bit_register_2_out;
  wire [11:8] AC_out_3;
  wire [15:0] alu_ac_inprselect_1_out16bit, bus1_1_out_10, controlled_buffer_2_out, controlled_buffer_3_out,
       DR_out, IR_out, n16bit_alu_1_out, TR_out;

  // Probe on in_1
  Clock clock_1 (.out(clock_1_out));
  Button button_1 (.out(button_1_out));
  _12bit_register u_12bit_register_1 (
    .clk(button_1_out), .\input (in_1), .out(n12bit_register_1_out), .ld(1'b1));  // open: inc, clr
  // Probe on n12bit_register_1_out
  microprg_contrl microprg_contrl_1 (
    .DR(DR_out), .AC({AC_out_4, AC_out_3, AC_out_2, AC_out}), .bus1_out(microprg_contrl_1_bus1_out),
    .out_10(microprg_contrl_1_out_10), .INCAC(microprg_contrl_1_incac), .LDAC(microprg_contrl_1_ldac),
    .WRITE(microprg_contrl_1_write), .out_13(microprg_contrl_1_out_13), .out_15(microprg_contrl_1_out_15),
    .out_16(microprg_contrl_1_out_16), .out_17(microprg_contrl_1_out_17), .out_18(microprg_contrl_1_out_18),
    .out_19(microprg_contrl_1_out_19), .out_20(microprg_contrl_1_out_20), .CLRAR(microprg_contrl_1_clrar),
    .out_26(microprg_contrl_1_out_26), .out_27(microprg_contrl_1_out_27), .LDDR(microprg_contrl_1_lddr),
    .LDIR(microprg_contrl_1_ldir), .\bus2_sel__ır_ld (\microprg_contrl_1_bus2_sel__ır_ld ),
    .E(n16bit_alu_1_c_out), .IR(IR_out), .inp_ld(microprg_contrl_1_inp_ld), .clk(clock_1_out), .fgi(FGI),
    .out_8(microprg_contrl_1_out_8), .fgo(FGO));
  assign controlled_buffer_1_out = or_1_out ? ar_pc_bus2_1_out : 12'bz;  // Controlled_Buffer controlled_buffer_1
  or or_1 (or_1_out, microprg_contrl_1_out_15, microprg_contrl_1_write);
  AR_PC_BUS2 ar_pc_bus2_1 (
    .in1(n12bit_register_2_out), .in0(AR_out), .s(\microprg_contrl_1_bus2_sel__ır_ld ), .out(ar_pc_bus2_1_out));
  // Probe on AR_out
  _12bit_register AR (
    .clk(clock_1_out), .\input (bus1_1_out_10[11:0]), .out(AR_out), .ld(microprg_contrl_1_out_10),
    .inc(microprg_contrl_1_incac), .clr(microprg_contrl_1_ldac));
  bus1 bus1_1 (
    .in_9(microprg_contrl_1_bus1_out), .out_10(bus1_1_out_10), ._1(AR_out), ._2(n12bit_register_2_out),
    ._3(DR_out), ._4({AC_out_4, AC_out_3, AC_out_2, AC_out}), ._5(IR_out), ._6(TR_out),
    ._7(controlled_buffer_3_out));  // open: _0
  assign controlled_buffer_2_out = not_1_out ? bus1_1_out_10 : 16'bz;  // Controlled_Buffer controlled_buffer_2
  RAM #(.addrWidth(12), .dataWidth(16)) ram_1 (
    .addr(controlled_buffer_1_out), .data(controlled_buffer_2_out), .sel(or_1_out), .clk(clock_1_out),
    .ld(microprg_contrl_1_out_15));  // open: clr
  not not_1 (not_1_out, microprg_contrl_1_out_15);
  // Probe on microprg_contrl_1_bus1_out
  assign controlled_buffer_3_out = microprg_contrl_1_out_15 ? controlled_buffer_2_out : 16'bz;  // Controlled_Buffer controlled_buffer_3
  // Probe on n12bit_register_2_out
  _12bit_register u_12bit_register_2 (
    .clk(clock_1_out), .\input (bus1_1_out_10[11:0]), .out(n12bit_register_2_out),
    .ld(microprg_contrl_1_out_19), .inc(microprg_contrl_1_out_17), .clr(microprg_contrl_1_out_18));
  // Probe on DR_out
  _16bit_register DR (
    .clk(clock_1_out), .\input (bus1_1_out_10), .out(DR_out), .ld(microprg_contrl_1_lddr),
    .inc(microprg_contrl_1_out_16));  // open: clr
  _8bit_register INPR (
    .clk(clock_1_out), .\input (\input ), .out(INPR_out), .ld(microprg_contrl_1_inp_ld));  // open: inc, clr
  alu_ac_inprSelect alu_ac_inprselect_1 (
    .in16bit({AC_out_4, AC_out_3, AC_out_2, AC_out}), .in8bit(INPR_out),
    ._16_8_select(microprg_contrl_1_inp_ld), .out16bit(alu_ac_inprselect_1_out16bit));
  _8bit_register OUTR (
    .clk(clock_1_out), .\input (bus1_1_out_10[7:0]), .out(\output ), .ld(microprg_contrl_1_out_13));  // open: inc, clr
  _16bit_alu u_16bit_alu_1 (
    .out(n16bit_alu_1_out), .c_out(n16bit_alu_1_c_out), .a(DR_out), .b(alu_ac_inprselect_1_out16bit),
    .s(microprg_contrl_1_out_8), .c_in(1'b0));
  Hex_Digit_Display hex_digit_display_1 (.value(bus1_1_out_10[15:12]));  // open: dp
  Hex_Digit_Display hex_digit_display_2 (.value(bus1_1_out_10[11:8]));  // open: dp
  Hex_Digit_Display hex_digit_display_3 (.value(AC_out_4));  // open: dp
  _16bit_register AC (
    .clk(clock_1_out), .\input (n16bit_alu_1_out), .out({AC_out_4, AC_out_3, AC_out_2, AC_out}),
    .ld(microprg_contrl_1_out_26), .inc(microprg_contrl_1_out_27), .clr(microprg_contrl_1_clrar));
  Hex_Digit_Display hex_digit_display_4 (.value(bus1_1_out_10[7:4]));  // open: dp
  Hex_Digit_Display hex_digit_display_5 (.value(bus1_1_out_10[3:0]));  // open: dp
  Hex_Digit_Display hex_digit_display_6 (.value(AC_out_3));  // open: dp
  Hex_Digit_Display hex_digit_display_7 (.value(AC_out_2));  // open: dp
  Hex_Digit_Display hex_digit_display_8 (.value(AC_out));  // open: dp
  // Probe on IR_out
  _16bit_register IR (
    .clk(clock_1_out), .\input (bus1_1_out_10), .out(IR_out), .ld(microprg_contrl_1_ldir));  // open: inc, clr
  _16bit_register TR (
    .clk(clock_1_out), .\input (bus1_1_out_10), .out(TR_out), .ld(microprg_contrl_1_out_20));  // open: inc, clr
  // Probe on TR_out

  // Notes on the sheet:
  //   7
  //   1
  //   PC
  //   s
  //   2
  //   3
  //   4
  //   5
  //   6
endmodule
