// Logisim project mux.circ as structural Verilog: 11 circuits, main circuit 2-1mux
module _2_1mux (
  input  in0,
  input  s,
  input  in1,
  output o
);

  wire nand_1_out, nand_2_out, not_1_out;

  nand nand_1 (nand_1_out, in0, not_1_out);
  not not_1 (not_1_out, s);
  nand nand_2 (nand_2_out, s, in1);
  nand nand_3 (o, nand_1_out, nand_2_out);
endmodule

module _4_1mux (
  input  _0,
  input  _1,
  input  _2,
  input  s1,
  input  _3,
  input  s0,
  output out_7
);

  wire n2_1mux_1_o, n2_1mux_2_o;

  _2_1mux u_2_1mux_1 (.in0(_0), .s(s0), .in1(_1), .o(n2_1mux_1_o));
  _2_1mux u_2_1mux_2 (.in0(_2), .s(s0), .in1(_3), .o(n2_1mux_2_o));
  _2_1mux u_2_1mux_3 (.in0(n2_1mux_1_o), .s(s1), .in1(n2_1mux_2_o), .o(out_7));
endmodule

module _2bit_adder (
  input  x,
  input  y,
  input  cin,
  output s,
  output cout
);

  wire and_1_out, and_2_out, xor_1_out;

  xor xor_1 (xor_1_out, x, y);
  and and_1 (and_1_out, x, y);
  xor xor_2 (s, xor_1_out, cin);
  and and_2 (and_2_out, cin, xor_1_out);
  or or_1 (cout, and_2_out, and_1_out);
endmodule

module _1bit_arith (
  input  c_in,
  input  a,
  input  b,
  input  s1,
  input  s0,
  output d,
  output c_out
);

  wire n4_1mux_1_out_7, not_1_out;

  not not_1 (not_1_out, b);
  _4_1mux u_4_1mux_1 (._0(b), ._1(not_1_out), ._2(1'b0), ._3(1'b1), .out_7(n4_1mux_1_out_7), .s0(s0), .s1(s1));
  _2bit_adder u_2bit_adder_1 (.x(a), .y(n4_1mux_1_out_7), .cin(c_in), .s(d), .cout(c_out));
endmodule

module _1bit_logic (
  input  a,
  input  b,
  input  s2,
  input  s1,
  input  s0,
  output o
);

  wire and_1_out, n4_1mux_1_out_7, n4_1mux_2_out_7, not_1_out, not_2_out, not_3_out, not_4_out, or_1_out,
       xor_1_out;

  and and_1 (and_1_out, a, b);
  or or_1 (or_1_out, a, b);
  xor xor_1 (xor_1_out, a, b);
  _4_1mux u_4_1mux_1 (
    ._0(and_1_out), ._1(not_1_out), ._2(or_1_out), ._3(not_2_out), .out_7(n4_1mux_1_out_7), .s0(s0), .s1(s1));
  not not_1 (not_1_out, and_1_out);
  not not_2 (not_2_out, or_1_out);
  _4_1mux u_4_1mux_2 (
    ._0(xor_1_out), ._1(not_3_out), ._2(not_4_out), ._3(a), .out_7(n4_1mux_2_out_7), .s0(s0), .s1(s1));
  not not_3 (not_3_out, xor_1_out);
  not not_4 (not_4_out, a);
  _2_1mux u_2_1mux_1 (.in0(n4_1mux_1_out_7), .s(s2), .in1(n4_1mux_2_out_7), .o(o));
endmodule

module _1bit_ariht_logic (
  input  c_in,
  input  a,
  input  b,
  input  s2,
  input  s1,
  input  s0,
  output d,
  output c_out,
  output o
);

  _1bit_arith u_1bit_arith_1 (.a(a), .b(b), .d(d), .c_out(c_out), .c_in(c_in), .s1(s1), .s0(s0));
  _1bit_logic u_1bit_logic_1 (.a(a), .b(b), .o(o), .s1(s1), .s0(s0), .s2(s2));
endmodule

module _4bit_arith_logic (
  input  [3:0] a,
  input  [3:0] b,
  input  c_in,
  input  [2:0] in_4,
  output [3:0] d,
  output [3:0] o,
  output c_ot
);

  wire n1bit_ariht_logic_1_c_out, n1bit_ariht_logic_2_c_out, n1bit_ariht_logic_3_c_out;

  _1bit_ariht_logic u_1bit_ariht_logic_1 (
    .a(a[0]), .b(b[0]), .d(d[0]), .c_out(n1bit_ariht_logic_1_c_out), .o(o[0]), .c_in(c_in), .s2(in_4[2]),
    .s1(in_4[1]), .s0(in_4[0]));
  _1bit_ariht_logic u_1bit_ariht_logic_2 (
    .a(a[1]), .b(b[1]), .d(d[1]), .c_out(n1bit_ariht_logic_2_c_out), .o(o[1]),
    .c_in(n1bit_ariht_logic_1_c_out), .s2(in_4[2]), .s1(in_4[1]), .s0(in_4[0]));
  _1bit_ariht_logic u_1bit_ariht_logic_3 (
    .a(a[2]), .b(b[2]), .d(d[2]), .c_out(n1bit_ariht_logic_3_c_out), .o(o[2]),
    .c_in(n1bit_ariht_logic_2_c_out), .s2(in_4[2]), .s1(in_4[1]), .s0(in_4[0]));
  _1bit_ariht_logic u_1bit_ariht_logic_4 (
    .a(a[3]), .b(b[3]), .d(d[3]), .c_out(c_ot), .o(o[3]), .c_in(n1bit_ariht_logic_3_c_out), .s2(in_4[2]),
    .s1(in_4[1]), .s0(in_4[0]));
endmodule

module _16bit_arith_logic (
  input  c_in,
  input  [15:0] a_16,
  input  [15:0] b_16,
  input  [2:0] s_3,
  output [15:0] d_16,
  output [15:0] o_16,
  output c_out
);

  wire n4bit_arith_logic_1_c_ot, n4bit_arith_logic_2_c_ot, n4bit_arith_logic_3_c_ot;

  _4bit_arith_logic u_4bit_arith_logic_1 (
    .d(d_16[3:0]), .o(o_16[3:0]), .c_ot(n4bit_arith_logic_1_c_ot), .a(a_16[3:0]), .b(b_16[3:0]), .c_in(c_in),
    .in_4(s_3));
  _4bit_arith_logic u_4bit_arith_logic_2 (
    .d(d_16[7:4]), .o(o_16[7:4]), .c_ot(n4bit_arith_logic_2_c_ot), .a(a_16[7:4]), .b(b_16[7:4]),
    .c_in(n4bit_arith_logic_1_c_ot), .in_4(s_3));
  _4bit_arith_logic u_4bit_arith_logic_3 (
    .d(d_16[11:8]), .o(o_16[11:8]), .c_ot(n4bit_arith_logic_3_c_ot), .a(a_16[11:8]), .b(b_16[11:8]),
    .c_in(n4bit_arith_logic_2_c_ot), .in_4(s_3));
  _4bit_arith_logic u_4bit_arith_logic_4 (
    .d(d_16[15:12]), .o(o_16[15:12]), .c_ot(c_out), .a(a_16[15:12]), .b(b_16[15:12]),
    .c_in(n4bit_arith_logic_3_c_ot), .in_4(s_3));
endmodule

module ssd (
  input  [15:0] in_1
);

  wire n2_1mux_1_o, n2_1mux_2_o, n2_1mux_3_o, n2_1mux_4_o, n2_1mux_5_o, n2_1mux_6_o, n2_1mux_7_o,
       n2_1mux_8_o, n2_1mux_9_o, n2_1mux_10_o, n2_1mux_11_o, n2_1mux_12_o, n2_1mux_13_o, n2_1mux_14_o,
       n2_1mux_15_o, n2_1mux_16_o, n2_1mux_17_o, n2_1mux_18_o, n2_1mux_19_o, undriven, undriven_2,
       undriven_3, undriven_4;

  _2_1mux u_2_1mux_1 (.in0(undriven_2), .in1(undriven_3), .o(n2_1mux_1_o));  // open: s
  _2_1mux u_2_1mux_2 (.in0(undriven), .in1(n2_1mux_1_o), .o(n2_1mux_2_o));  // open: s
  _2_1mux u_2_1mux_3 (.o(n2_1mux_3_o));  // open: in0, s, in1
  _2_1mux u_2_1mux_4 (.in0(n2_1mux_2_o), .s(undriven_4), .o(n2_1mux_4_o));  // open: in1
  _2_1mux u_2_1mux_5 (.s(undriven_4), .o(n2_1mux_5_o));  // open: in0, in1
  _2_1mux u_2_1mux_6 (.s(undriven_4), .o(n2_1mux_6_o));  // open: in0, in1
  _2_1mux u_2_1mux_7 (.s(undriven_4), .o(n2_1mux_7_o));  // open: in0, in1
  _2_1mux u_2_1mux_8 (.s(undriven_4), .o(n2_1mux_8_o));  // open: in0, in1
  _2_1mux u_2_1mux_9 (.s(undriven_4), .o(n2_1mux_9_o));  // open: in0, in1
  _2_1mux u_2_1mux_10 (.s(undriven_4), .o(n2_1mux_10_o));  // open: in0, in1
  _2_1mux u_2_1mux_11 (.s(undriven_4), .o(n2_1mux_11_o));  // open: in0, in1
  _2_1mux u_2_1mux_12 (.s(undriven_4), .o(n2_1mux_12_o));  // open: in0, in1
  _2_1mux u_2_1mux_13 (.s(undriven_4), .o(n2_1mux_13_o));  // open: in0, in1
  _2_1mux u_2_1mux_14 (.s(undriven_4), .o(n2_1mux_14_o));  // open: in0, in1
  _2_1mux u_2_1mux_15 (.s(undriven_4), .o(n2_1mux_15_o));  // open: in0, in1
  _2_1mux u_2_1mux_16 (.s(undriven_4), .o(n2_1mux_16_o));  // open: in0, in1
  _2_1mux u_2_1mux_17 (.s(undriven_4), .o(n2_1mux_17_o));  // open: in0, in1
  _2_1mux u_2_1mux_18 (.s(undriven_4), .o(n2_1mux_18_o));  // open: in0, in1
  _2_1mux u_2_1mux_19 (.s(undriven_4), .in1(n2_1mux_3_o), .o(n2_1mux_19_o));  // open: in0
endmodule

module _1bit_a_l_s (
  input  c_in,
  input  a,
  input  b,
  input  a_1,
  input  a_1_2,
  input  s3,
  input  s2,
  input  s1,
  input  s0,
  output f,
  output c_out
);

  wire n1bit_arith_1_d, n1bit_logic_1_o;

  _1bit_arith u_1bit_arith_1 (.a(a), .b(b), .d(n1bit_arith_1_d), .c_out(c_out), .c_in(c_in), .s1(s1), .s0(s0));
  _1bit_logic u_1bit_logic_1 (.a(a), .b(b), .o(n1bit_logic_1_o), .s1(s1), .s0(s0), .s2(s2));
  _4_1mux u_4_1mux_1 (._0(n1bit_arith_1_d), ._1(n1bit_logic_1_o), ._2(a_1), ._3(a_1_2), .out_7(f), .s0(s2), .s1(s3));
endmodule

module sdas (
  input  [15:0] in_1,
  input  [15:0] in_2
);

  wire n1bit_a_l_s_1_c_out, n1bit_a_l_s_2_p1, n1bit_a_l_s_2_p2, n1bit_a_l_s_2_p3, n1bit_a_l_s_2_p4,
       n1bit_a_l_s_2_p6, n1bit_a_l_s_3_p2, n1bit_a_l_s_3_p4, n1bit_a_l_s_3_p6, n1bit_a_l_s_4_p2,
       n1bit_a_l_s_4_p4;

  _1bit_a_l_s u_1bit_a_l_s_1 (
    .c_out(n1bit_a_l_s_1_c_out), .a_1(n1bit_a_l_s_2_p1), .a_1_2(n1bit_a_l_s_2_p3));  // open: a, b, f, c_in, s3, s2, s1, s0
  // _1bit_a_l_s 1bit_a_l_s_2: pin names not known; wires that end beside it: n1bit_a_l_s_2_p1, n1bit_a_l_s_2_p2, n1bit_a_l_s_2_p3, n1bit_a_l_s_2_p4, n1bit_a_l_s_1_c_out, n1bit_a_l_s_2_p6
  // _1bit_a_l_s 1bit_a_l_s_3: pin names not known; wires that end beside it: n1bit_a_l_s_2_p2, n1bit_a_l_s_3_p2, n1bit_a_l_s_2_p4, n1bit_a_l_s_3_p4, n1bit_a_l_s_2_p6, n1bit_a_l_s_3_p6
  // _1bit_a_l_s 1bit_a_l_s_4: pin names not known; wires that end beside it: n1bit_a_l_s_3_p2, n1bit_a_l_s_4_p2, n1bit_a_l_s_3_p4, n1bit_a_l_s_4_p4, n1bit_a_l_s_3_p6
endmodule
