// Logisim project prj2.circ as structural Verilog: 2 circuits, main circuit main
module main (
  input  d,
  input  en,
  output q,
  output q_prime
);

  wire and_1_out, and_2_out, not_1_out;

  not not_1 (not_1_out, d);
  and and_1 (and_1_out, not_1_out, en);
  and and_2 (and_2_out, en, d);
  nor nor_1 (q, and_1_out, q_prime);
  nor nor_2 (q_prime, q, and_2_out);
endmodule

module r (
);

  main main_1 ();  // open: d, en, q, q_prime
endmodule
