// Logisim project prj4tasl.circ as structural Verilog: 1 circuit, main circuit main
module main (
  input  [11:0] in_1,
  input  [15:0] IR,
  output [3:0] out_3,
  output [7:0] map
);

  wire and_1_out, undriven;
  wire [1:0] multiplexer_1_out, multiplexer_2_out;
  wire [3:0] priority_encoder_2_out;
  wire [23:0] rom_1_data;

  // Probe on IR
  Priority_Encoder #(.select(4)) priority_encoder_1 (
    .in0(in_1[0]), .in1(in_1[1]), .in2(in_1[2]), .in3(in_1[3]), .in4(in_1[4]), .in5(in_1[5]), .in6(in_1[6]),
    .in7(in_1[7]), .in8(in_1[8]), .in9(in_1[9]), .in10(in_1[10]), .in11(in_1[11]), .out(out_3));  // open: in12, in13, in14, in15, gs, en_out, en_in
  Priority_Encoder #(.select(4)) priority_encoder_2 (
    .in0(IR[0]), .in1(IR[1]), .in2(IR[2]), .in3(IR[3]), .in4(IR[4]), .in5(IR[5]), .in6(IR[6]), .in7(IR[7]),
    .in8(IR[8]), .in9(IR[9]), .in10(IR[10]), .in11(IR[11]), .in12(1'b0), .in13(1'b0), .in14(1'b0),
    .in15(1'b0), .out(priority_encoder_2_out), .en_in(undriven));  // open: gs, en_out
  Multiplexer #(.width(2)) multiplexer_1 (.in0(2'b01), .in1(2'b10), .out(multiplexer_1_out), .sel(IR[15]));  // open: en
  Multiplexer #(.width(2)) multiplexer_2 (
    .in0(2'b00), .in1(multiplexer_1_out), .out(multiplexer_2_out), .sel(IR[12]));  // open: en
  and and_1 (and_1_out, IR[12], IR[13], IR[14]);
  // Probe on map
  Multiplexer #(.width(8)) multiplexer_3 (
    .in0({3'b000, IR[14:12], 2'b00}), .in1({multiplexer_2_out, priority_encoder_2_out, 2'b00}), .out(map),
    .sel(and_1_out));  // open: en
  ROM #(.dataWidth(24)) rom_1 (.addr(map), .data(rom_1_data));  // open: sel

  // Notes on the sheet:
  //   indrt
  //   mem ref
  //   reg-ref/io
endmodule
