// Logisim project project_alu - Kopya.circ as structural Verilog: 10 circuits, main circuit alu-test
module _2_1mux (
  input  in0,
  input  s,
  input  in1,
  output o
);

  wire nand_1_out, nand_2_out, not_1_out;

  nand nand_1 (nand_1_out, in0, not_1_out);
  not not_1 (not_1_out, s);
  nand nand_2 (nand_2_out, s, in1);
  nand nand_3 (o, nand_1_out, nand_2_out);
endmodule

module _4_1mux (
  input  _0,
  input  _1,
  input  _2,
  input  s1,
  input  _3,
  input  s0,
  output out_7
);

  wire n2_1mux_1_o, n2_1mux_2_o;

  _2_1mux u_2_1mux_1 (.in0(_0), .s(s0), .in1(_1), .o(n2_1mux_1_o));
  _2_1mux u_2_1mux_2 (.in0(_2), .s(s0), .in1(_3), .o(n2_1mux_2_o));
  _2_1mux u_2_1mux_3 (.in0(n2_1mux_1_o), .s(s1), .in1(n2_1mux_2_o), .o(out_7));
endmodule

module _2bit_adder (
  input  x,
  input  y,
  input  cin,
  output s,
  output cout
);

  wire and_1_out, and_2_out, xor_1_out;

  xor xor_1 (xor_1_out, x, y);
  and and_1 (and_1_out, x, y);
  xor xor_2 (s, xor_1_out, cin);
  and and_2 (and_2_out, cin, xor_1_out);
  or or_1 (cout, and_2_out, and_1_out);
endmodule

module _1bit_arith (
  input  c_in,
  input  a,
  input  b,
  input  s1,
  input  s0,
  output d,
  output c_out
);

  wire n4_1mux_1_out_7, not_1_out;

  not not_1 (not_1_out, b);
  _4_1mux u_4_1mux_1 (._0(b), ._1(not_1_out), ._2(1'b0), ._3(1'b1), .out_7(n4_1mux_1_out_7), .s0(s0), .s1(s1));
  _2bit_adder u_2bit_adder_1 (.x(a), .y(n4_1mux_1_out_7), .cin(c_in), .s(d), .cout(c_out));
endmodule

module _1bit_logic (
  input  a,
  input  b,
  input  s2,
  input  s1,
  input  s0,
  output o
);

  wire and_1_out, n4_1mux_1_out_7, n4_1mux_2_out_7, not_1_out, not_2_out, not_3_out, not_4_out, or_1_out,
       xor_1_out;

  and and_1 (and_1_out, a, b);
  or or_1 (or_1_out, a, b);
  xor xor_1 (xor_1_out, a, b);
  _4_1mux u_4_1mux_1 (
    ._0(and_1_out), ._1(not_1_out), ._2(or_1_out), ._3(not_2_out), .out_7(n4_1mux_1_out_7), .s0(s0), .s1(s1));
  not not_1 (not_1_out, and_1_out);
  not not_2 (not_2_out, or_1_out);
  _4_1mux u_4_1mux_2 (
    ._0(xor_1_out), ._1(not_3_out), ._2(not_4_out), ._3(a), .out_7(n4_1mux_2_out_7), .s0(s0), .s1(s1));
  not not_3 (not_3_out, xor_1_out);
  not not_4 (not_4_out, a);
  _2_1mux u_2_1mux_1 (.in0(n4_1mux_1_out_7), .s(s2), .in1(n4_1mux_2_out_7), .o(o));
endmodule

module _1bit_ariht_logic (
  input  c_in,
  input  a,
  input  b,
  input  s2,
  input  s1,
  input  s0,
  output d,
  output c_out,
  output o
);

  _1bit_arith u_1bit_arith_1 (.a(a), .b(b), .d(d), .c_out(c_out), .c_in(c_in), .s1(s1), .s0(s0));
  _1bit_logic u_1bit_logic_1 (.a(a), .b(b), .o(o), .s1(s1), .s0(s0), .s2(s2));
endmodule

module _1bit_a_l_s (
  input  c_in,
  input  a,
  input  b,
  input  a_1,
  input  a_1_2,
  input  s3,
  input  s2,
  input  s1,
  input  s0,
  output f,
  output c_out
);

  wire n1bit_arith_1_d, n1bit_logic_1_o;

  _1bit_arith u_1bit_arith_1 (.a(a), .b(b), .d(n1bit_arith_1_d), .c_out(c_out), .c_in(c_in), .s1(s1), .s0(s0));
  _1bit_logic u_1bit_logic_1 (.a(a), .b(b), .o(n1bit_logic_1_o), .s1(s1), .s0(s0), .s2(s2));
  _4_1mux u_4_1mux_1 (._0(n1bit_arith_1_d), ._1(n1bit_logic_1_o), ._2(a_1), ._3(a_1_2), .out_7(f), .s0(s2), .s1(s3));
endmodule

module _4bit_a_l_s (
  input  [3:0] a,
  input  [3:0] b,
  input  c_in,
  input  [3:0] s,
  input  [3:0] a_1,
  input  [3:0] a_1_2,
  output [3:0] o,
  output c_out
);

  wire _2_c_out, n1bit_a_l_s_1_c_out, n1bit_a_l_s_2_c_out;

  _1bit_a_l_s u_1bit_a_l_s_1 (
    .a(a[0]), .b(b[0]), .f(o[0]), .c_out(n1bit_a_l_s_1_c_out), .c_in(c_in), .s3(s[3]), .s2(s[2]), .s1(s[1]),
    .s0(s[0]), .a_1(a_1[0]), .a_1_2(a_1_2[0]));
  _1bit_a_l_s u_1bit_a_l_s_2 (
    .a(a[1]), .b(b[1]), .f(o[1]), .c_out(n1bit_a_l_s_2_c_out), .c_in(n1bit_a_l_s_1_c_out), .s3(s[3]),
    .s2(s[2]), .s1(s[1]), .s0(s[0]), .a_1(a_1[1]), .a_1_2(a_1_2[1]));
  _1bit_a_l_s _2 (
    .a(a[2]), .b(b[2]), .f(o[2]), .c_out(_2_c_out), .c_in(n1bit_a_l_s_2_c_out), .s3(s[3]), .s2(s[2]),
    .s1(s[1]), .s0(s[0]), .a_1(a_1[2]), .a_1_2(a_1_2[2]));
  _1bit_a_l_s u_1bit_a_l_s_3 (
    .a(a[3]), .b(b[3]), .f(o[3]), .c_out(c_out), .c_in(_2_c_out), .s3(s[3]), .s2(s[2]), .s1(s[1]), .s0(s[0]),
    .a_1(a_1[3]), .a_1_2(a_1_2[3]));
endmodule

module _16bit_alu (
  input  c_in,
  input  [3:0] s,
  input  [15:0] a,
  input  [15:0] b,
  output [15:0] out,
  output c_out
);

  wire n4bit_a_l_s_1_c_out, n4bit_a_l_s_2_c_out, n4bit_a_l_s_3_c_out;
  wire [0:0] n2_1mux_1_o;
  wire [3:3] n4_1mux_1_out_7;

  _2_1mux u_2_1mux_1 (.in0(a[15]), .s(s[0]), .in1(1'b0), .o(n2_1mux_1_o[0]));
  _4bit_a_l_s u_4bit_a_l_s_1 (
    .s(s), .o(out[3:0]), .a(a[3:0]), .b(b[3:0]), .c_in(c_in), .a_1({a[2:0], n2_1mux_1_o[0]}), .a_1_2(a[4:1]),
    .c_out(n4bit_a_l_s_1_c_out));
  _4bit_a_l_s u_4bit_a_l_s_2 (
    .s(s), .o(out[7:4]), .a(a[7:4]), .b(b[7:4]), .c_in(n4bit_a_l_s_1_c_out), .a_1(a[6:3]), .a_1_2(a[8:5]),
    .c_out(n4bit_a_l_s_2_c_out));
  _4bit_a_l_s u_4bit_a_l_s_3 (
    .s(s), .o(out[11:8]), .a(a[11:8]), .b(b[11:8]), .c_in(n4bit_a_l_s_2_c_out), .a_1(a[10:7]),
    .a_1_2(a[12:9]), .c_out(n4bit_a_l_s_3_c_out));
  _4bit_a_l_s u_4bit_a_l_s_4 (
    .s(s), .o(out[15:12]), .a(a[15:12]), .b(b[15:12]), .c_in(n4bit_a_l_s_3_c_out), .a_1(a[14:11]),
    .a_1_2({n4_1mux_1_out_7[3], a[15:13]}), .c_out(c_out));
  _4_1mux u_4_1mux_1 (._0(1'b0), ._1(a[0]), ._2(a[15]), .out_7(n4_1mux_1_out_7[3]), .s0(s[0]), .s1(s[1]));  // open: _3
endmodule

module alu_test (
  input  c_in,
  input  [15:0] a,
  input  [15:0] b,
  input  [3:0] s,
  output [15:0] out,
  output c_out
);

  _16bit_alu u_16bit_alu_1 (.out(out), .c_out(c_out), .a(a), .b(b), .s(s), .c_in(c_in));
endmodule
