// Logisim project 2-4decoder-2.circ as structural Verilog: 1 circuit, main circuit main
module main (
  input  i1,
  input  i0,
  output o0,
  output o1,
  output o2,
  output o3
);

  wire not_1_out, not_2_out, not_3_out, not_4_out;

  not not_1 (not_1_out, i1);
  not not_2 (not_2_out, i0);
  not not_3 (not_3_out, i1);
  not not_4 (not_4_out, i0);
  and and_1 (o3, i1, i0);
  and and_2 (o0, not_1_out, not_2_out);
  and and_3 (o1, not_3_out, i0);
  and and_4 (o2, i1, not_4_out);
endmodule
