// Logisim project hw4.circ as structural Verilog: 1 circuit, main circuit main
module main (
  input  d,
  input  _0,
  input  _1,
  input  [1:0] bc,
  input  [1:0] _0a,
  output f
);

  wire multiplexer_1_out, multiplexer_3_out, not_1_out;

  not not_1 (not_1_out, d);
  Multiplexer #(.select(2), .enable("false")) multiplexer_1 (
    .in0(_0), .in1(_1), .in2(d), .in3(not_1_out), .out(multiplexer_1_out), .sel(bc));
  Multiplexer #(.select(2), .enable("false")) multiplexer_2 (
    .in0(multiplexer_1_out), .in1(multiplexer_3_out), .out(f), .sel(_0a));  // open: in2, in3
  Multiplexer #(.select(2), .enable("false")) multiplexer_3 (
    .in0(not_1_out), .in1(_1), .in2(_0), .in3(d), .out(multiplexer_3_out), .sel(bc));
endmodule
