// Logisim project hw4q1-son.circ as structural Verilog: 1 circuit, main circuit main
module main (
  input  _1,
  input  [3:0] B,
  input  [3:0] A,
  input  _1_2,
  input  [3:0] C,
  output [3:0] A_B,
  output f3,
  output f2,
  output f1,
  output [3:0] A_C
);

  wire adder_1_cout, adder_2_cout, main_1_o1, main_1_o2;
  wire [3:0] not_1_out, not_2_out;

  assign not_1_out = ~B;  // NOT_Gate not_1, 4 bits wide
  assign not_2_out = ~C;  // NOT_Gate not_2, 4 bits wide
  Adder #(.width(4)) adder_1 (.a(not_1_out), .b(A), .out(A_B), .cin(_1), .cout(adder_1_cout));
  Adder #(.width(4)) adder_2 (.a(A), .b(not_2_out), .out(A_C), .cin(_1_2), .cout(adder_2_cout));
  _2_4decoder_2_main main_1 (.i1(adder_1_cout), .i0(adder_2_cout), .o0(f3), .o1(main_1_o1), .o2(main_1_o2), .o3(f1));
  or or_1 (f2, main_1_o1, main_1_o2);

  // Notes on the sheet:
  //   0
  //   1
  //   2
  //   3
endmodule
