// Logisim project hw4q1.circ as structural Verilog: 1 circuit, main circuit main
module main (
  input  _1,
  input  [3:0] B,
  input  [3:0] A,
  input  _1_2,
  input  [3:0] C,
  output [3:0] s1,
  output f3,
  output f2,
  output f1,
  output [3:0] s2
);

  wire and_3_out, decoder_1_out1, decoder_1_out2, decoder_1_out3, or_1_out, X1_out, X2_out;
  wire [1:0] adder_1_cout;
  wire [3:0] not_1_out, not_2_out;

  assign not_1_out = ~B;  // NOT_Gate not_1, 4 bits wide
  assign not_2_out = ~C;  // NOT_Gate not_2, 4 bits wide
  Adder #(.width(4)) adder_1 (.a(not_1_out), .b(A), .out(s1), .cin(_1), .cout(adder_1_cout[0]));
  Decoder #(.select(2), .enable("false")) decoder_1 (
    .out0(f3), .out1(decoder_1_out1), .out2(decoder_1_out2), .out3(decoder_1_out3), .sel(adder_1_cout));
  Adder #(.width(4)) adder_2 (.a(A), .b(not_2_out), .out(s2), .cin(_1_2), .cout(adder_1_cout[1]));
  or X1 (X1_out, s1[0], s1[1], s1[2], s1[3]);
  or X2 (X2_out, s2[0], s2[1], s2[2], s2[3]);
  or or_1 (or_1_out, decoder_1_out1, decoder_1_out2);
  and and_1 (f2, or_1_out, and_3_out);
  and and_2 (f1, decoder_1_out3, X1_out);
  and and_3 (and_3_out, X1_out, X2_out);

  // Notes on the sheet:
  //   C1
  //   C2
endmodule
