// Logisim project lab8.circ as structural Verilog: 7 circuits, main circuit main
module main (
  input  in_1,
  input  a,
  input  in_3,
  input  b,
  input  in_5,
  input  a_2,
  input  b_2,
  input  b_3,
  output out_9,
  output out_10
);

  wire and_1_out, and_2_out, clock_1_out, not_1_out, not_2_out, or_1_out, xor_1_out;

  Multiplexer multiplexer_1 (.in0(a), .in1(not_1_out), .sel(in_3));  // open: out, en
  not not_1 (not_1_out, a);
  Multiplexer multiplexer_2 (.in0(b), .in1(not_2_out), .sel(in_5));  // open: out, en
  not not_2 (not_2_out, b);
  Adder #(.width(1)) adder_1 (.cin(in_1));  // open: a, b, out, cout
  and and_1 (and_1_out, a_2, b_2);
  xor xor_1 (xor_1_out, a_2, b_2);
  ExactlyOne xor_2 (.out(out_9), .in0(a_2), .in1(b_2), .in2(out_10));
  Clock clock_1 (.out(clock_1_out));
  and and_2 (and_2_out, xor_1_out, out_10);
  D_Flip_Flop d_ff_1 (.clk(clock_1_out), .D(or_1_out), .Q(out_10));  // open: Qn, preset, en, reset
  or or_1 (or_1_out, and_1_out, and_2_out);
  Shift_Register #(.length(4)) shift_register_1 (
    .in(out_9), .clk(clock_1_out));  // open: shift, out, load, clr, d0, q0, d1, q1, d2, q2, d3, q3
endmodule

module alu (
  input  A,
  input  B,
  input  [2:0] s2_s1_s0,
  input  E,
  output \Ç ,
  output Cout
);

  wire multiplexer_1_out, multiplexer_2_out, multiplexer_3_out, not_1_out, not_2_out;

  not not_1 (not_1_out, A);
  Multiplexer #(.select(3)) multiplexer_1 (
    .in0(A), .in1(A), .in2(A), .in3(not_1_out), .in4(A), .in5(not_1_out), .in6(1'b0), .in7(1'b0),
    .out(multiplexer_1_out), .sel(s2_s1_s0));  // open: en
  Multiplexer multiplexer_2 (.in0(E), .in1(1'b0), .out(multiplexer_2_out), .sel(s2_s1_s0[2]));  // open: en
  Adder #(.width(1)) adder_1 (
    .a(multiplexer_1_out), .b(multiplexer_3_out), .out(\Ç ), .cin(multiplexer_2_out), .cout(Cout));
  not not_2 (not_2_out, B);
  Multiplexer #(.select(3)) multiplexer_3 (
    .in0(B), .in1(not_2_out), .in2(1'b0), .in3(1'b0), .in4(B), .in5(1'b0), .in6(B), .in7(1'b0),
    .out(multiplexer_3_out), .sel(s2_s1_s0));  // open: en
endmodule

module asd (
  input  A,
  input  B,
  input  [2:0] s2_s1_s0,
  output [3:0] _4bit_out
);

  wire alu_1_cout, \alu_1_ç , clock_1_out, clr_out, d_ff_1_q;

  Clock clock_1 (.out(clock_1_out));
  alu alu_1 (.s2_s1_s0(s2_s1_s0), .E(d_ff_1_q), .\Ç (\alu_1_ç ), .A(A), .B(B), .Cout(alu_1_cout));
  D_Flip_Flop d_ff_1 (.clk(clock_1_out), .D(alu_1_cout), .Q(d_ff_1_q));  // open: Qn, preset, en, reset
  Button clr (.out(clr_out));
  D_Flip_Flop o3 (.clk(clock_1_out), .D(\alu_1_ç ), .Q(_4bit_out[3]), .reset(clr_out));  // open: Qn, preset, en
  D_Flip_Flop o1 (.clk(clock_1_out), .D(_4bit_out[2]), .Q(_4bit_out[1]), .reset(clr_out));  // open: Qn, preset, en
  D_Flip_Flop o2 (.clk(clock_1_out), .D(_4bit_out[3]), .Q(_4bit_out[2]), .reset(clr_out));  // open: Qn, preset, en
  D_Flip_Flop o0 (.clk(clock_1_out), .D(_4bit_out[1]), .Q(_4bit_out[0]), .reset(clr_out));  // open: Qn, preset, en
endmodule

module asdsad (
  input  [3:0] in_1,
  input  [3:0] in_2,
  input  in_3,
  input  shift___load,
  input  [3:0] in_5,
  input  in_6,
  output [3:0] out_7
);

  wire \alu_1_ç , clock_1_out, not_1_out, not_2_out, not_3_out, shift_register_1_q0, shift_register_2_q0,
       shift_register_3_out, shift_register_3_q0, shift_register_3_q1, shift_register_3_q2,
       shift_register_3_q3;
  wire [1:0] counter_1_q;

  Counter #(.width(2), .max('h3)) counter_1 (
    .count(clock_1_out), .Q(counter_1_q), .clk(clock_1_out));  // open: load, D, carry, clr
  Clock clock_1 (.out(clock_1_out));
  not not_1 (not_1_out, shift___load);
  Shift_Register #(.length(4)) shift_register_1 (
    .shift(not_1_out), .in(in_3), .clk(clock_1_out), .load(shift___load), .d0(in_1[3]),
    .q0(shift_register_1_q0), .d1(in_1[2]), .d2(in_1[1]), .d3(in_1[0]));  // open: out, clr, q1, q2, q3
  not not_2 (not_2_out, shift___load);
  Shift_Register #(.length(4)) shift_register_2 (
    .shift(not_2_out), .in(in_6), .clk(clock_1_out), .load(shift___load), .d0(in_5[3]),
    .q0(shift_register_2_q0), .d1(in_5[2]), .d2(in_5[1]), .d3(in_5[0]));  // open: out, clr, q1, q2, q3
  Shifter #(.width(4)) shifter_1 (.in(in_1), .\dist (counter_1_q), .out(out_7));
  not not_3 (not_3_out, shift___load);
  Shift_Register #(.length(4)) shift_register_3 (
    .shift(not_3_out), .in(\alu_1_ç ), .clk(clock_1_out), .out(shift_register_3_out), .load(shift___load),
    .d0(in_2[3]), .q0(shift_register_3_q0), .d1(in_2[2]), .q1(shift_register_3_q1), .d2(in_2[1]),
    .q2(shift_register_3_q2), .d3(in_2[0]), .q3(shift_register_3_q3));  // open: clr
  alu alu_1 (
    .E(shift_register_3_out), .\Ç (\alu_1_ç ), .A(shift_register_1_q0), .B(shift_register_2_q0));  // open: s2_s1_s0, Cout
endmodule

module multiplier (
  input  [3:0] A,
  input  [7:0] B,
  output [3:0] out_3,
  output [7:0] out_4,
  output [7:0] \output 
);

  wire clock_1_out, clr_out;
  wire [1:0] counter_q;
  wire [7:0] shift_register_q7;

  Clock clock_1 (.out(clock_1_out));
  Counter #(.width(2), .max('h3)) counter (
    .count(clock_1_out), .Q(counter_q), .clk(clock_1_out), .clr(clr_out));  // open: load, D, carry
  Button clr (.out(clr_out));
  Shifter #(.width(4), .shift("lr")) shifter_1 (.in(A), .\dist (counter_q), .out(out_3));
  Shifter shifter_2 (.in(B), .\dist ({1'b0, counter_q}), .out(out_4));
  Shift_Register shift_register (
    .shift(1'b0), .in(1'b0), .clk(clock_1_out), .load(out_3[0]), .clr(clr_out), .d0(out_4[7]),
    .q0(shift_register_q7[7]), .d1(out_4[6]), .q1(shift_register_q7[6]), .d2(out_4[5]),
    .q2(shift_register_q7[5]), .d3(out_4[4]), .q3(shift_register_q7[4]), .d4(out_4[3]),
    .q4(shift_register_q7[3]), .d5(out_4[2]), .q5(shift_register_q7[2]), .d6(out_4[1]),
    .q6(shift_register_q7[1]), .d7(out_4[0]), .q7(shift_register_q7[0]));  // open: out
  result_hold result_hold_1 (.in(shift_register_q7), .clk(clock_1_out), .clear(clr_out), .out(\output ));

  // Notes on the sheet:
  //   counter
  //   right shifter
  //   left shifter
endmodule

module result_hold (
  input  [7:0] in,
  input  clk,
  input  clear,
  output [7:0] out
);

  wire or_1_out, or_2_out, or_3_out, or_4_out, or_5_out, or_6_out, or_7_out, or_8_out;

  or or_1 (or_1_out, in[0], out[0]);
  or or_2 (or_2_out, in[1], out[1]);
  or or_3 (or_3_out, in[2], out[2]);
  or or_4 (or_4_out, in[3], out[3]);
  or or_5 (or_5_out, in[4], out[4]);
  or or_6 (or_6_out, in[5], out[5]);
  or or_7 (or_7_out, in[6], out[6]);
  or or_8 (or_8_out, in[7], out[7]);
  D_Flip_Flop d_ff_1 (.clk(clk), .D(or_1_out), .Q(out[0]), .reset(clear));  // open: Qn, preset, en
  D_Flip_Flop d_ff_2 (.clk(clk), .D(or_2_out), .Q(out[1]), .reset(clear));  // open: Qn, preset, en
  D_Flip_Flop d_ff_3 (.clk(clk), .D(or_3_out), .Q(out[2]), .reset(clear));  // open: Qn, preset, en
  D_Flip_Flop d_ff_4 (.clk(clk), .D(or_4_out), .Q(out[3]), .reset(clear));  // open: Qn, preset, en
  D_Flip_Flop d_ff_5 (.clk(clk), .D(or_5_out), .Q(out[4]), .reset(clear));  // open: Qn, preset, en
  D_Flip_Flop d_ff_6 (.clk(clk), .D(or_6_out), .Q(out[5]), .reset(clear));  // open: Qn, preset, en
  D_Flip_Flop d_ff_7 (.clk(clk), .D(or_7_out), .Q(out[6]), .reset(clear));  // open: Qn, preset, en
  D_Flip_Flop d_ff_8 (.clk(clk), .D(or_8_out), .Q(out[7]), .reset(clear));  // open: Qn, preset, en
endmodule

module m2 (
  input  [3:0] A,
  input  [7:0] B,
  output [3:0] out_rightShift,
  output [7:0] \output ,
  output [7:0] out_leftShift,
  output out_6
);

  wire clock_1_out, clr_out, not_1_out;
  wire [1:0] counter_q;
  wire [7:0] shift_register__1_q7, shift_register__2_q7;

  Clock clock_1 (.out(clock_1_out));
  Counter #(.width(2), .max('h3), .ongoal("continue")) counter (
    .count(clock_1_out), .Q(counter_q), .clk(clock_1_out), .clr(clr_out));  // open: load, D, carry
  Button clr (.out(clr_out));
  Shifter #(.width(4), .shift("lr")) shifter_1 (.in(A), .\dist (counter_q), .out(out_rightShift));
  Shifter shifter_2 (.in(B), .\dist ({1'b0, counter_q}), .out(out_leftShift));
  not not_1 (not_1_out, clock_1_out);
  Shift_Register shift_register__1 (
    .shift(1'b0), .in(1'b0), .clk(not_1_out), .load(out_rightShift[0]), .clr(clr_out), .d0(out_leftShift[7]),
    .q0(shift_register__1_q7[7]), .d1(out_leftShift[6]), .q1(shift_register__1_q7[6]), .d2(out_leftShift[5]),
    .q2(shift_register__1_q7[5]), .d3(out_leftShift[4]), .q3(shift_register__1_q7[4]), .d4(out_leftShift[3]),
    .q4(shift_register__1_q7[3]), .d5(out_leftShift[2]), .q5(shift_register__1_q7[2]), .d6(out_leftShift[1]),
    .q6(shift_register__1_q7[1]), .d7(out_leftShift[0]), .q7(shift_register__1_q7[0]));  // open: out
  Adder adder_1 (.a(shift_register__2_q7), .b(shift_register__1_q7), .out(\output ), .cin(1'b0), .cout(out_6));
  Shift_Register shift_register__2 (
    .shift(1'b0), .in(1'b0), .clk(not_1_out), .load(out_rightShift[0]), .clr(clr_out), .d0(\output [7]),
    .q0(shift_register__2_q7[7]), .d1(\output [6]), .q1(shift_register__2_q7[6]), .d2(\output [5]),
    .q2(shift_register__2_q7[5]), .d3(\output [4]), .q3(shift_register__2_q7[4]), .d4(\output [3]),
    .q4(shift_register__2_q7[3]), .d5(\output [2]), .q5(shift_register__2_q7[2]), .d6(\output [1]),
    .q6(shift_register__2_q7[1]), .d7(\output [0]), .q7(shift_register__2_q7[0]));  // open: out

  // Notes on the sheet:
  //   right shifter
  //   left shifter
endmodule
